// Logisim project Lab1.circ as structural Verilog: 6 circuits, main circuit main
module main (
);

  wire clock_1_out, romseq_1_out, sequentialinput_1_notdone, sequentialinput_1_x;
  wire [2:0] combinational_1_out_9, romcomb_1_out_2;
  wire [7:0] combinationalinput_1_in0;

  SequentialInput sequentialinput_1 (.X(sequentialinput_1_x), .NotDone(sequentialinput_1_notdone), .Clock(clock_1_out));
  // Probe on sequentialinput_1_x
  Clock clock_1 (.out(clock_1_out));
  ROMSeq romseq_1 (.X(sequentialinput_1_x), .sel(sequentialinput_1_notdone), .Clock(clock_1_out), .Out(romseq_1_out));
  CombinationalInput combinationalinput_1 (
    .In7(combinationalinput_1_in0[7]), .In6(combinationalinput_1_in0[6]), .In5(combinationalinput_1_in0[5]),
    .In4(combinationalinput_1_in0[4]), .In3(combinationalinput_1_in0[3]), .In2(combinationalinput_1_in0[2]),
    .In1(combinationalinput_1_in0[1]), .In0(combinationalinput_1_in0[0]), .Clock(clock_1_out));
  // Probe on romseq_1_out
  // Probe on combinationalinput_1_in0
  Combinational combinational_1 (
    .In7(combinationalinput_1_in0[7]), .In6(combinationalinput_1_in0[6]), .In5(combinationalinput_1_in0[5]),
    .In4(combinationalinput_1_in0[4]), .In3(combinationalinput_1_in0[3]), .In2(combinationalinput_1_in0[2]),
    .In1(combinationalinput_1_in0[1]), .In0(combinationalinput_1_in0[0]), .out_9(combinational_1_out_9));
  ROMComb romcomb_1 (.in_1(combinationalinput_1_in0), .out_2(romcomb_1_out_2));
  // Probe on combinational_1_out_9
  // Probe on romcomb_1_out_2
endmodule

module Combinational (
  input  In7,
  input  In6,
  input  In5,
  input  In4,
  input  In3,
  input  In2,
  input  In1,
  input  In0,
  output [2:0] out_9
);

  wire and_1_out, and_2_out, and_3_out, and_4_out, and_5_out, and_6_out, and_7_out, and_8_out, and_9_out,
       and_10_out, not_1_out, not_2_out, not_3_out, not_4_out, not_5_out, not_6_out, not_7_out, not_8_out,
       not_9_out, not_10_out, not_11_out, not_12_out, not_13_out, not_14_out, not_15_out, not_16_out,
       not_17_out, not_18_out, not_19_out, not_20_out, not_21_out, not_22_out, not_23_out, not_24_out,
       not_25_out, not_26_out, not_27_out, not_28_out, not_29_out, not_30_out, not_31_out, not_32_out,
       not_33_out, not_34_out, not_35_out, not_36_out, not_37_out;

  not not_1 (not_1_out, In7);
  not not_2 (not_2_out, In6);
  not not_3 (not_3_out, In5);
  not not_4 (not_4_out, In4);
  not not_5 (not_5_out, In3);
  not not_6 (not_6_out, In7);
  not not_7 (not_7_out, In6);
  not not_8 (not_8_out, In5);
  not not_9 (not_9_out, In4);
  not not_10 (not_10_out, In2);
  not not_11 (not_11_out, In0);
  not not_12 (not_12_out, In7);
  not not_13 (not_13_out, In6);
  not not_14 (not_14_out, In5);
  not not_15 (not_15_out, In4);
  not not_16 (not_16_out, In3);
  not not_17 (not_17_out, In1);
  not not_18 (not_18_out, In5);
  not not_19 (not_19_out, In7);
  not not_20 (not_20_out, In5);
  not not_21 (not_21_out, In4);
  not not_22 (not_22_out, In2);
  not not_23 (not_23_out, In7);
  not not_24 (not_24_out, In5);
  not not_25 (not_25_out, In4);
  not not_26 (not_26_out, In1);
  not not_27 (not_27_out, In7);
  not not_28 (not_28_out, In5);
  not not_29 (not_29_out, In4);
  not not_30 (not_30_out, In0);
  not not_31 (not_31_out, In7);
  not not_32 (not_32_out, In5);
  not not_33 (not_33_out, In4);
  not not_34 (not_34_out, In7);
  not not_35 (not_35_out, In5);
  not not_36 (not_36_out, In4);
  not not_37 (not_37_out, In5);
  and and_1 (and_1_out, not_1_out, not_2_out, not_3_out, not_4_out, not_5_out, In2, In1, In0);
  and and_2 (and_2_out, not_6_out, not_7_out, not_8_out, not_9_out, In3, not_10_out, In1, not_11_out);
  and and_3 (and_3_out, not_12_out, not_13_out, not_14_out, not_15_out, not_16_out, In2, not_17_out);
  and and_4 (and_4_out, In7, In6, not_18_out);
  and and_5 (and_5_out, not_19_out, not_20_out, not_21_out, not_22_out, In0);
  and and_6 (and_6_out, not_23_out, not_24_out, not_25_out, not_26_out, In0);
  and and_7 (and_7_out, not_27_out, not_28_out, not_29_out, In1, not_30_out);
  and and_8 (and_8_out, not_31_out, not_32_out, not_33_out, In3);
  and and_9 (and_9_out, not_34_out, In6, not_35_out, not_36_out);
  and and_10 (and_10_out, In7, In6, not_37_out, In4);
  or or_1 (out_9[2], and_1_out, and_2_out);
  or or_2 (out_9[1], and_3_out, and_4_out);
  or or_3 (out_9[0], and_5_out, and_6_out, and_7_out, and_8_out, and_9_out, and_10_out);
endmodule

module ROMComb (
  input  [7:0] in_1,
  output [2:0] out_2
);

  ROM #(.dataWidth(3)) rom_1 (.addr(in_1), .data(out_2));  // open: sel

  // Notes on the sheet:
  //   contents of rom_1 (hex, n*v repeats v):
  //   0 0 1 0 2 3 0 4 4 0 5 53*0 16*1 112*0 16*2 16*3
endmodule

module ROMSeq (
  input  X,
  input  sel,
  input  Clock,
  output Out
);

  wire [3:0] register_1_q;
  wire [4:0] rom_1_data;

  ROM #(.addrWidth(5), .dataWidth(5)) rom_1 (.addr({register_1_q, X}), .data(rom_1_data), .sel(sel));
  Register #(.width(5)) register_1 (.D(rom_1_data), .Q({register_1_q, Out}), .clk(Clock));  // open: en, clr

  // Notes on the sheet:
  //   contents of rom_1 (hex, n*v repeats v):
  //   a 2 c 4 6 6 8 8 b 3 e c 10 6 12 10 14 8 14 14 a 2
endmodule

module SequentialInput (
  input  Clock,
  output X,
  output NotDone
);

  wire comparator_1_eq, counter_2_q;
  wire [5:0] counter_1_q;

  Counter #(.width(6), .max('h3f), .ongoal("stay")) counter_1 (
    .count(1'b1), .Q(counter_1_q), .clk(Clock));  // open: load, D, carry, clr
  Comparator #(.width(6)) comparator_1 (.a(counter_1_q), .b({6{1'b1}}), .eq(comparator_1_eq));  // open: gt, lt
  ROM #(.addrWidth(6), .dataWidth(1)) rom_1 (.addr(counter_1_q), .data(X));  // open: sel
  Counter #(.width(1), .max('h1), .ongoal("stay")) counter_2 (
    .count(comparator_1_eq), .Q(counter_2_q), .clk(Clock));  // open: load, D, carry, clr
  not not_1 (NotDone, counter_2_q);

  // Notes on the sheet:
  //   contents of rom_1 (hex, n*v repeats v):
  //   7*0 1 0 0 1 0 0 0 1 1 0 1 0 0 0 1 0 1 0 1 1 0 0 4*1 0 0 0 1 0 0 1 1 0 1 0 1 0 4*1 0 0 1 1 0 4*1 0
  //   4*1
endmodule

module CombinationalInput (
  input  Clock,
  output In7,
  output In6,
  output In5,
  output In4,
  output In3,
  output In2,
  output In1,
  output In0
);

  wire [7:0] counter_1_q;

  Counter #(.ongoal("stay")) counter_1 (.count(1'b1), .Q(counter_1_q), .clk(Clock));  // open: load, D, carry, clr
  ROM rom_1 (.addr(counter_1_q), .data({In7, In6, In5, In4, In3, In2, In1, In0}));  // open: sel

  // Notes on the sheet:
  //   contents of rom_1 (hex, n*v repeats v):
  //   0 1 2 3 4 5 6 7 8 9 a b c d e f 10 11 12 13 14 15 16 17 18 19 1a 1b 1c 1d 1e 1f 20 21 22 23 24 25 26
  //   27 28 29 2a 2b 2c 2d 2e 2f 30 31 32 33 34 35 36 37 38 39 3a 3b 3c 3d 3e 3f 40 41 42 43 44 45 46 47
  //   48 49 4a 4b 4c 4d 4e 4f 50 51 52 53 54 55 56 57 58 59 5a 5b 5c 5d 5e 5f 60 61 62 63 64 65 66 67 68
  //   69 6a 6b 6c 6d 6e 6f 70 71 72 73 74 75 76 77 78 79 7a 7b 7c 7d 7e 7f 80 81 82 83 84 85 86 87 88 89
  //   8a 8b 8c 8d 8e 8f 90 91 92 93 94 95 96 97 98 99 9a 9b 9c 9d 9e 9f a0 a1 a2 a3 a4 a5 a6 a7 a8 a9 aa
  //   ab ac ad ae af b0 b1 b2 b3 b4 b5 b6 b7 b8 b9 ba bb bc bd be bf c0 c1 c2 c3 c4 c5 c6 c7 c8 c9 ca cb
  //   cc cd ce cf d0 d1 d2 d3 d4 d5 d6 d7 d8 d9 da db dc dd de df e0 e1 e2 e3 e4 e5 e6 e7 e8 e9 ea eb ec
  //   ed ee ef f0 f1 f2 f3 f4 f5 f6 f7 f8 f9 fa fb fc fd fe ff
endmodule
