// Logisim project WriteControl.circ as structural Verilog: 2 circuits, main circuit WriteControl
module WriteControl (
  input  In31,
  input  In30,
  input  In29,
  input  In28,
  input  In27,
  input  In26,
  output TristateBuffer,
  output ReadMem,
  output Beq,
  output Jump
);

  wire not_1_out, not_2_out, not_3_out, not_4_out, not_5_out, not_6_out, not_7_out, not_8_out, not_9_out,
       not_10_out, not_11_out, not_12_out, not_13_out, not_14_out, not_15_out;

  not not_1 (not_1_out, In30);
  not not_2 (not_2_out, In28);
  not not_3 (not_3_out, In30);
  not not_4 (not_4_out, In29);
  not not_5 (not_5_out, In28);
  not not_6 (not_6_out, In31);
  not not_7 (not_7_out, In30);
  not not_8 (not_8_out, In29);
  not not_9 (not_9_out, In27);
  not not_10 (not_10_out, In26);
  not not_11 (not_11_out, In31);
  not not_12 (not_12_out, In30);
  not not_13 (not_13_out, In29);
  not not_14 (not_14_out, In28);
  not not_15 (not_15_out, In26);
  and and_1 (TristateBuffer, In31, not_1_out, In29, not_2_out, In27, In26);
  and and_2 (ReadMem, In31, not_3_out, not_4_out, not_5_out, In27, In26);
  and and_3 (Beq, not_6_out, not_7_out, not_8_out, In28, not_9_out, not_10_out);
  and and_4 (Jump, not_11_out, not_12_out, not_13_out, not_14_out, In27, not_15_out);
endmodule

module RightControl (
  input  In31,
  input  In30,
  input  In29,
  input  In28,
  input  In27,
  input  In26,
  output TristateBuffer,
  output ReadMem,
  output Beq,
  output Jump
);

  wire not_1_out, not_2_out, not_3_out, not_4_out, not_5_out, not_6_out, not_7_out, not_8_out, not_9_out,
       not_10_out, not_11_out, not_12_out, not_13_out, not_14_out, not_15_out;

  not not_1 (not_1_out, In30);
  not not_2 (not_2_out, In28);
  not not_3 (not_3_out, In30);
  not not_4 (not_4_out, In29);
  not not_5 (not_5_out, In28);
  not not_6 (not_6_out, In31);
  not not_7 (not_7_out, In30);
  not not_8 (not_8_out, In29);
  not not_9 (not_9_out, In27);
  not not_10 (not_10_out, In26);
  not not_11 (not_11_out, In31);
  not not_12 (not_12_out, In30);
  not not_13 (not_13_out, In29);
  not not_14 (not_14_out, In28);
  not not_15 (not_15_out, In26);
  and and_1 (TristateBuffer, In31, not_1_out, In29, not_2_out, In27, In26);
  and and_2 (ReadMem, In31, not_3_out, not_4_out, not_5_out, In27, In26);
  and and_3 (Beq, not_6_out, not_7_out, not_8_out, In28, not_9_out, not_10_out);
  and and_4 (Jump, not_11_out, not_12_out, not_13_out, not_14_out, In27, not_15_out);
endmodule
