// Logisim project MultiCycleMips_CorrectALU.circ as structural Verilog: 8 circuits, main circuit main
module main (
);

  wire ALUSrcA, and_1_out, Clock, comparator_1_eq, comparator_2_eq, controlunit_1_pcwrite,
       controlunit_1_pcwritecond, IorD, IRWrite, MemRead, MemtoReg, MemWrite, not_1_out, or_2_out, PCen,
       RegDst, RegWrite, zero;
  wire [1:0] ALUSrcB, PCSource;
  wire [3:0] alucontrolnew_1_o0, multiplexer_6_out;
  wire [4:0] multiplexer_3_out, Shamt;
  wire [5:0] Funct, Opcode;
  wire [6:0] bit_extender_1_out, bit_extender_2_out;
  wire [7:0] multiplexer_1_out;
  wire [25:11] IR_q;
  wire [31:0] A_q, alu_1_aluresult, ALUout_q, bit_extender_3_out, bit_extender_4_out, MDR_q,
       multiplexer_2_out, multiplexer_4_out, multiplexer_5_out, NewPC, ram_1_data, register_1_q,
       registerfile_1_read_data1, registerfile_1_read_data2, shifter_1_out, shifter_2_out, Store;

  Bit_Extender #(.in_width(32), .out_width(7)) bit_extender_1 (.in(register_1_q), .out(bit_extender_1_out));
  Register #(.width(32)) register_1 (.D(NewPC), .en(PCen), .Q(register_1_q), .clk(Clock));  // open: clr
  Bit_Extender #(.in_width(32), .out_width(7)) bit_extender_2 (.in(ALUout_q), .out(bit_extender_2_out));
  Clock clock_1 (.out(Clock));
  or or_1 (PCen, and_1_out, controlunit_1_pcwrite);
  Multiplexer #(.width(8), .enable("false")) multiplexer_1 (
    .in0({1'b0, bit_extender_1_out}), .in1({1'b1, bit_extender_2_out}), .out(multiplexer_1_out), .sel(IorD));
  and and_1 (and_1_out, zero, controlunit_1_pcwritecond);
  not not_1 (not_1_out, MemWrite);
  RAM #(.dataWidth(32)) ram_1 (
    .addr(multiplexer_1_out), .data(ram_1_data), .clk(Clock), .ld(not_1_out));  // open: sel, clr
  assign ram_1_data = MemWrite ? Store : 32'bz;  // Controlled_Buffer controlled_buffer_1
  Register #(.width(32)) MDR (.D(ram_1_data), .Q(MDR_q), .clk(Clock));  // open: en, clr
  Register #(.width(32)) IR (.D(ram_1_data), .en(IRWrite), .Q({Opcode, IR_q, Shamt, Funct}), .clk(Clock));  // open: clr
  ControlUnit controlunit_1 (
    .Opcode(Opcode), .Clock(Clock), .PCWriteCond(controlunit_1_pcwritecond), .PCWrite(controlunit_1_pcwrite),
    .IRWrite(IRWrite), .ALUSrcA(ALUSrcA), .IORD(IorD), .PCSource(PCSource), .ALUSrcB(ALUSrcB),
    .RegDST(RegDst), .MemtoReg(MemtoReg), .MemRead(MemRead), .MemWrite(MemWrite), .RegWrite(RegWrite));
  RegisterFile registerfile_1 (
    .WriteData(multiplexer_2_out), .ReadReg2(IR_q[20:16]), .RegWrite(RegWrite), .WriteReg(multiplexer_3_out),
    .Read_Data2(registerfile_1_read_data2), .Read_Data1(registerfile_1_read_data1), .clock(Clock),
    .Read_Reg1(IR_q[25:21]));
  Multiplexer #(.width(32), .enable("false")) multiplexer_2 (
    .in0(ALUout_q), .in1(MDR_q), .out(multiplexer_2_out), .sel(MemtoReg));
  Multiplexer #(.width(5), .enable("false")) multiplexer_3 (
    .in0(IR_q[20:16]), .in1(IR_q[15:11]), .out(multiplexer_3_out), .sel(RegDst));
  assign bit_extender_3_out = {{16{IR_q[15]}}, {IR_q[15:11], Shamt, Funct}};  // Bit_Extender bit_extender_3
  assign bit_extender_4_out = {{6{IR_q[25]}}, {IR_q, Shamt, Funct}};  // Bit_Extender bit_extender_4
  Shifter #(.width(32)) shifter_1 (.in(bit_extender_4_out), .\dist (5'b00010), .out(shifter_1_out));
  Shifter #(.width(32)) shifter_2 (.in(bit_extender_3_out), .\dist (5'b00010), .out(shifter_2_out));
  Comparator #(.width(2), .mode("unsigned")) comparator_1 (
    .a(2'b11), .b(ALUSrcB), .eq(comparator_1_eq));  // open: gt, lt
  Comparator #(.width(2), .mode("unsigned")) comparator_2 (
    .a(2'b01), .b(ALUSrcB), .eq(comparator_2_eq));  // open: gt, lt
  Register #(.width(32)) A (.D(registerfile_1_read_data1), .Q(A_q), .clk(Clock));  // open: en, clr
  Register #(.width(32)) B (.D(registerfile_1_read_data2), .Q(Store), .clk(Clock));  // open: en, clr
  ALUControlNew alucontrolnew_1 (
    .i0(Funct[0]), .i1(Funct[1]), .i2(Funct[2]), .i3(Funct[3]), .i4(Funct[4]), .i5(Funct[5]),
    .i26(Opcode[0]), .i27(Opcode[1]), .i28(Opcode[2]), .i29(Opcode[3]), .i30(Opcode[4]), .i31(Opcode[5]),
    .o0(alucontrolnew_1_o0[0]), .o1(alucontrolnew_1_o0[1]), .o2(alucontrolnew_1_o0[2]),
    .o3(alucontrolnew_1_o0[3]));
  Multiplexer #(.width(32), .enable("false")) multiplexer_4 (
    .in0(register_1_q), .in1(A_q), .out(multiplexer_4_out), .sel(ALUSrcA));
  Multiplexer #(.select(2), .width(32), .enable("false")) multiplexer_5 (
    .in0(Store), .in1(32'h4), .in2(bit_extender_3_out), .in3(shifter_2_out), .out(multiplexer_5_out),
    .sel(ALUSrcB));
  or or_2 (or_2_out, comparator_1_eq, comparator_2_eq);
  Multiplexer #(.width(4), .enable("false")) multiplexer_6 (
    .in0(alucontrolnew_1_o0), .in1(4'b0010), .out(multiplexer_6_out), .sel(or_2_out));
  ALU alu_1 (
    .ALUCtl(multiplexer_6_out), .A(multiplexer_4_out), .B(multiplexer_5_out), .ALUResult(alu_1_aluresult),
    .Zero(zero), .SHamt(Shamt));  // open: Overflow
  Multiplexer #(.select(2), .width(32), .enable("false")) multiplexer_7 (
    .in0(alu_1_aluresult), .in1(ALUout_q), .in2(shifter_1_out), .out(NewPC), .sel(PCSource));  // open: in3
  Register #(.width(32)) ALUout (.D(alu_1_aluresult), .Q(ALUout_q), .clk(Clock));  // open: en, clr

  // Notes on the sheet:
  //   PCWrite
  //   PCWriteCond
  //   ControlUnit
endmodule

module _32bit (
  input  Add_Sub_control,
  input  [31:0] in_2,
  input  [31:0] in_3,
  output [31:0] out_4,
  output carry_out
);

  wire adder_1_cout, subtractor_1_bout;
  wire [31:0] adder_1_out, subtractor_1_out;

  Adder #(.width(32)) adder_1 (.a(in_2), .b(in_3), .out(adder_1_out), .cout(adder_1_cout));  // open: cin
  Subtractor #(.width(32)) subtractor_1 (
    .a(in_2), .b(in_3), .out(subtractor_1_out), .bout(subtractor_1_bout));  // open: bin
  Multiplexer #(.width(32), .enable("false")) multiplexer_1 (
    .in0(adder_1_out), .in1(subtractor_1_out), .out(out_4), .sel(Add_Sub_control));
  Multiplexer #(.enable("false")) multiplexer_2 (
    .in0(adder_1_cout), .in1(subtractor_1_bout), .out(carry_out), .sel(Add_Sub_control));
endmodule

module ALU (
  input  [3:0] ALUCtl,
  input  [31:0] A,
  input  [31:0] B,
  input  [4:0] SHamt,
  output [31:0] ALUResult,
  output Zero,
  output Overflow
);

  wire and_2_out, and_3_out, comparator_1_lt, not_1_out, not_2_out, not_4_out, not_5_out, not_6_out,
       or_2_out, or_3_out, xor_1_out;
  wire [31:0] AND_out, bit_extender_1_out, multiplexer_1_out, multiplexer_2_out, multiplexer_4_out,
       n32bit_1_out_4, not_3_out, OR_out, shifter_1_out, shifter_2_out;

  _32bit u_32bit_1 (.Add_Sub_control(ALUCtl[2]), .in_2(A), .in_3(B), .out_4(n32bit_1_out_4));  // open: carry_out
  xor xor_1 (xor_1_out, ALUCtl[2], B[31]);
  not not_1 (not_1_out, A[31]);
  assign OR_out = A | B;  // OR_Gate OR, 32 bits wide
  assign AND_out = A & B;  // AND_Gate AND, 32 bits wide
  Comparator #(.width(32)) comparator_1 (.a(A), .b(B), .lt(comparator_1_lt));  // open: gt, eq
  not not_2 (not_2_out, xor_1_out);
  Shifter #(.width(32)) shifter_1 (.in(B), .\dist (SHamt), .out(shifter_1_out));
  Shifter #(.width(32), .shift("lr")) shifter_2 (.in(B), .\dist (SHamt), .out(shifter_2_out));
  assign not_3_out = ~OR_out;  // NOT_Gate not_3, 32 bits wide
  assign bit_extender_1_out = {{31{1'b0}}, comparator_1_lt};  // Bit_Extender bit_extender_1
  Multiplexer #(.width(32), .enable("false")) multiplexer_1 (
    .in0(AND_out), .in1(OR_out), .out(multiplexer_1_out), .sel(ALUCtl[0]));
  not not_4 (not_4_out, n32bit_1_out_4[31]);
  and and_2 (and_2_out, A[31], not_4_out, xor_1_out);
  and and_3 (and_3_out, not_2_out, n32bit_1_out_4[31], not_1_out);
  Multiplexer #(.width(32), .enable("false")) multiplexer_2 (
    .in0(shifter_1_out), .in1(shifter_2_out), .out(multiplexer_2_out), .sel(ALUCtl[2]));
  Multiplexer #(.select(2), .width(32), .enable("false")) multiplexer_3 (
    .in0(multiplexer_1_out), .in1(multiplexer_4_out), .in2(not_3_out), .in3(multiplexer_2_out),
    .out(ALUResult), .sel({ALUCtl[3], ALUCtl[1]}));
  Multiplexer #(.width(32), .enable("false")) multiplexer_4 (
    .in0(n32bit_1_out_4), .in1(bit_extender_1_out), .out(multiplexer_4_out), .sel(ALUCtl[0]));
  or or_2 (or_2_out, and_2_out, and_3_out);
  not not_5 (not_5_out, ALUCtl[3]);
  not not_6 (not_6_out, ALUCtl[0]);
  and and_4 (Overflow, or_2_out, not_5_out, ALUCtl[1], not_6_out);
  or or_3 (or_3_out, ALUResult[0], ALUResult[1], ALUResult[2], ALUResult[3], ALUResult[4], ALUResult[5], ALUResult[6], ALUResult[7], ALUResult[8], ALUResult[9], ALUResult[10], ALUResult[11], ALUResult[12], ALUResult[13], ALUResult[14], ALUResult[15], ALUResult[16], ALUResult[17], ALUResult[18], ALUResult[19], ALUResult[20], ALUResult[21], ALUResult[22], ALUResult[23], ALUResult[24], ALUResult[25], ALUResult[26], ALUResult[27], ALUResult[28], ALUResult[29], ALUResult[30], ALUResult[31]);
  not not_7 (Zero, or_3_out);

  // Other names for the same wires on the sheet: ALUCtl_1 = ALUCtl[1]; ALUCtl_3 = ALUCtl[3]; ALUCtl_0 = ALUCtl[0];
  //   ALUCtl_2 = ALUCtl[2]
endmodule

module RegisterFile (
  input  clock,
  input  [31:0] WriteData,
  input  [4:0] ReadReg2,
  input  RegWrite,
  input  [4:0] Read_Reg1,
  input  [4:0] WriteReg,
  output [31:0] Read_Data2,
  output [31:0] Read_Data1
);

  wire demultiplexer_1_out0, demultiplexer_1_out1, demultiplexer_1_out2, demultiplexer_1_out3,
       demultiplexer_1_out4, demultiplexer_1_out5, demultiplexer_1_out6, demultiplexer_1_out7,
       demultiplexer_1_out8, demultiplexer_1_out9, demultiplexer_1_out10, demultiplexer_1_out11,
       demultiplexer_1_out12, demultiplexer_1_out13, demultiplexer_1_out14, demultiplexer_1_out15,
       demultiplexer_1_out16, demultiplexer_1_out17, demultiplexer_1_out18, demultiplexer_1_out19,
       demultiplexer_1_out20, demultiplexer_1_out21, demultiplexer_1_out22, demultiplexer_1_out23,
       demultiplexer_1_out24, demultiplexer_1_out25, demultiplexer_1_out26, demultiplexer_1_out27,
       demultiplexer_1_out28, demultiplexer_1_out29, demultiplexer_1_out30, demultiplexer_1_out31;
  wire [31:0] Reg0_2_q, Reg0_3_q, Reg0_4_q, Reg0_5_q, Reg0_6_q, Reg0_7_q, Reg0_8_q, Reg0_9_q, Reg0_10_q,
       Reg0_11_q, Reg0_12_q, Reg0_13_q, Reg0_14_q, Reg0_15_q, Reg0_16_q, Reg0_17_q, Reg0_18_q, Reg0_19_q,
       Reg0_20_q, Reg0_21_q, Reg0_22_q, Reg0_23_q, Reg0_24_q, Reg0_25_q, Reg0_26_q, Reg0_27_q, Reg0_28_q,
       Reg0_29_q, Reg0_30_q, Reg0_31_q, Reg0_32_q, Reg0_q;

  Demultiplexer #(.select(5), .enable("false")) demultiplexer_1 (
    .out0(demultiplexer_1_out0), .out1(demultiplexer_1_out1), .out2(demultiplexer_1_out2),
    .out3(demultiplexer_1_out3), .out4(demultiplexer_1_out4), .out5(demultiplexer_1_out5),
    .out6(demultiplexer_1_out6), .out7(demultiplexer_1_out7), .out8(demultiplexer_1_out8),
    .out9(demultiplexer_1_out9), .out10(demultiplexer_1_out10), .out11(demultiplexer_1_out11),
    .out12(demultiplexer_1_out12), .out13(demultiplexer_1_out13), .out14(demultiplexer_1_out14),
    .out15(demultiplexer_1_out15), .out16(demultiplexer_1_out16), .out17(demultiplexer_1_out17),
    .out18(demultiplexer_1_out18), .out19(demultiplexer_1_out19), .out20(demultiplexer_1_out20),
    .out21(demultiplexer_1_out21), .out22(demultiplexer_1_out22), .out23(demultiplexer_1_out23),
    .out24(demultiplexer_1_out24), .out25(demultiplexer_1_out25), .out26(demultiplexer_1_out26),
    .out27(demultiplexer_1_out27), .out28(demultiplexer_1_out28), .out29(demultiplexer_1_out29),
    .out30(demultiplexer_1_out30), .out31(demultiplexer_1_out31), .in(RegWrite), .sel(WriteReg));
  // Probe on WriteData
  Register #(.width(32)) Reg0 (.D(WriteData), .en(demultiplexer_1_out0), .Q(Reg0_q), .clk(clock));  // open: clr
  Register #(.width(32)) Reg0_2 (.D(WriteData), .en(demultiplexer_1_out4), .Q(Reg0_2_q), .clk(clock));  // open: clr
  Register #(.width(32)) Reg0_3 (.D(WriteData), .en(demultiplexer_1_out8), .Q(Reg0_3_q), .clk(clock));  // open: clr
  Register #(.width(32)) Reg0_4 (.D(WriteData), .en(demultiplexer_1_out12), .Q(Reg0_4_q), .clk(clock));  // open: clr
  Register #(.width(32)) Reg0_5 (.D(WriteData), .en(demultiplexer_1_out16), .Q(Reg0_5_q), .clk(clock));  // open: clr
  Register #(.width(32)) Reg0_6 (.D(WriteData), .en(demultiplexer_1_out20), .Q(Reg0_6_q), .clk(clock));  // open: clr
  Register #(.width(32)) Reg0_7 (.D(WriteData), .en(demultiplexer_1_out24), .Q(Reg0_7_q), .clk(clock));  // open: clr
  Register #(.width(32)) Reg0_8 (.D(WriteData), .en(demultiplexer_1_out28), .Q(Reg0_8_q), .clk(clock));  // open: clr
  Register #(.width(32)) Reg0_9 (.D(WriteData), .en(demultiplexer_1_out1), .Q(Reg0_9_q), .clk(clock));  // open: clr
  Register #(.width(32)) Reg0_10 (.D(WriteData), .en(demultiplexer_1_out5), .Q(Reg0_10_q), .clk(clock));  // open: clr
  Register #(.width(32)) Reg0_11 (.D(WriteData), .en(demultiplexer_1_out9), .Q(Reg0_11_q), .clk(clock));  // open: clr
  Register #(.width(32)) Reg0_12 (.D(WriteData), .en(demultiplexer_1_out13), .Q(Reg0_12_q), .clk(clock));  // open: clr
  Register #(.width(32)) Reg0_13 (.D(WriteData), .en(demultiplexer_1_out17), .Q(Reg0_13_q), .clk(clock));  // open: clr
  Register #(.width(32)) Reg0_14 (.D(WriteData), .en(demultiplexer_1_out21), .Q(Reg0_14_q), .clk(clock));  // open: clr
  Register #(.width(32)) Reg0_15 (.D(WriteData), .en(demultiplexer_1_out25), .Q(Reg0_15_q), .clk(clock));  // open: clr
  Register #(.width(32)) Reg0_16 (.D(WriteData), .en(demultiplexer_1_out29), .Q(Reg0_16_q), .clk(clock));  // open: clr
  Register #(.width(32)) Reg0_17 (.D(WriteData), .en(demultiplexer_1_out2), .Q(Reg0_17_q), .clk(clock));  // open: clr
  Register #(.width(32)) Reg0_18 (.D(WriteData), .en(demultiplexer_1_out6), .Q(Reg0_18_q), .clk(clock));  // open: clr
  Register #(.width(32)) Reg0_19 (.D(WriteData), .en(demultiplexer_1_out10), .Q(Reg0_19_q), .clk(clock));  // open: clr
  Register #(.width(32)) Reg0_20 (.D(WriteData), .en(demultiplexer_1_out14), .Q(Reg0_20_q), .clk(clock));  // open: clr
  Register #(.width(32)) Reg0_21 (.D(WriteData), .en(demultiplexer_1_out18), .Q(Reg0_21_q), .clk(clock));  // open: clr
  Register #(.width(32)) Reg0_22 (.D(WriteData), .en(demultiplexer_1_out22), .Q(Reg0_22_q), .clk(clock));  // open: clr
  Register #(.width(32)) Reg0_23 (.D(WriteData), .en(demultiplexer_1_out26), .Q(Reg0_23_q), .clk(clock), .clr(clock));
  Register #(.width(32)) Reg0_24 (.D(WriteData), .en(demultiplexer_1_out30), .Q(Reg0_24_q), .clk(clock));  // open: clr
  Register #(.width(32)) Reg0_25 (.D(WriteData), .en(demultiplexer_1_out3), .Q(Reg0_25_q), .clk(clock));  // open: clr
  Register #(.width(32)) Reg0_26 (.D(WriteData), .en(demultiplexer_1_out7), .Q(Reg0_26_q), .clk(clock));  // open: clr
  Register #(.width(32)) Reg0_27 (.D(WriteData), .en(demultiplexer_1_out11), .Q(Reg0_27_q), .clk(clock));  // open: clr
  Register #(.width(32)) Reg0_28 (.D(WriteData), .en(demultiplexer_1_out15), .Q(Reg0_28_q), .clk(clock));  // open: clr
  Register #(.width(32)) Reg0_29 (.D(WriteData), .en(demultiplexer_1_out19), .Q(Reg0_29_q), .clk(clock));  // open: clr
  Register #(.width(32)) Reg0_30 (.D(WriteData), .en(demultiplexer_1_out23), .Q(Reg0_30_q), .clk(clock));  // open: clr
  Register #(.width(32)) Reg0_31 (.D(WriteData), .en(demultiplexer_1_out27), .Q(Reg0_31_q), .clk(clock));  // open: clr
  Register #(.width(32)) Reg0_32 (.D(WriteData), .en(demultiplexer_1_out31), .Q(Reg0_32_q), .clk(clock));  // open: clr
  Multiplexer #(.select(5), .width(32)) multiplexer_1 (
    .in0(Reg0_q), .in1(Reg0_9_q), .in2(Reg0_17_q), .in3(Reg0_25_q), .in4(Reg0_2_q), .in5(Reg0_10_q),
    .in6(Reg0_18_q), .in7(Reg0_26_q), .in8(Reg0_3_q), .in9(Reg0_11_q), .in10(Reg0_19_q), .in11(Reg0_27_q),
    .in12(Reg0_4_q), .in13(Reg0_12_q), .in14(Reg0_20_q), .in15(Reg0_28_q), .in16(Reg0_5_q), .in17(Reg0_13_q),
    .in18(Reg0_21_q), .in19(Reg0_29_q), .in20(Reg0_6_q), .in21(Reg0_14_q), .in22(Reg0_22_q),
    .in23(Reg0_30_q), .in24(Reg0_7_q), .in25(Reg0_15_q), .in26(Reg0_23_q), .in27(Reg0_31_q), .in28(Reg0_8_q),
    .in29(Reg0_16_q), .in30(Reg0_24_q), .in31(Reg0_32_q), .out(Read_Data1), .sel(Read_Reg1));  // open: en
  Multiplexer #(.select(5), .width(32)) multiplexer_2 (
    .in0(Reg0_q), .in1(Reg0_9_q), .in2(Reg0_17_q), .in3(Reg0_25_q), .in4(Reg0_2_q), .in5(Reg0_10_q),
    .in6(Reg0_18_q), .in7(Reg0_26_q), .in8(Reg0_3_q), .in9(Reg0_11_q), .in10(Reg0_19_q), .in11(Reg0_27_q),
    .in12(Reg0_4_q), .in13(Reg0_12_q), .in14(Reg0_20_q), .in15(Reg0_28_q), .in16(Reg0_5_q), .in17(Reg0_13_q),
    .in18(Reg0_21_q), .in19(Reg0_29_q), .in20(Reg0_6_q), .in21(Reg0_14_q), .in22(Reg0_22_q),
    .in23(Reg0_30_q), .in24(Reg0_7_q), .in25(Reg0_15_q), .in26(Reg0_23_q), .in27(Reg0_31_q), .in28(Reg0_8_q),
    .in29(Reg0_16_q), .in30(Reg0_24_q), .in31(Reg0_32_q), .out(Read_Data2), .sel(ReadReg2));  // open: en
endmodule

module ALUControl (
  input  [5:0] Opcode,
  input  [5:0] Funct,
  output [3:0] ALUCtl
);

  wire and_1_out, and_2_out, and_3_out, and_4_out, and_5_out, and_6_out, and_7_out, and_8_out, and_9_out,
       and_10_out, and_11_out, and_12_out, and_13_out, and_14_out, and_15_out, and_16_out, and_17_out,
       and_18_out, and_19_out, and_20_out, and_21_out, and_22_out, and_23_out, and_24_out, and_25_out,
       and_26_out, and_27_out, and_28_out, and_29_out, and_30_out, and_31_out, and_32_out, and_33_out,
       and_34_out, and_35_out, and_36_out, and_37_out, and_38_out, and_39_out, and_40_out, and_41_out,
       and_42_out, and_43_out, and_44_out, and_45_out, and_46_out, and_47_out, and_48_out, and_49_out,
       and_50_out, and_51_out, and_52_out, nor_1_out, nor_2_out, nor_3_out, nor_4_out, not_1_out, not_2_out,
       not_3_out, not_4_out, not_5_out, not_6_out, not_7_out, not_8_out, not_9_out, not_10_out, not_11_out,
       not_12_out, not_13_out, not_14_out, not_15_out, not_16_out, not_17_out, not_18_out, not_19_out,
       not_20_out, not_21_out, not_22_out, not_23_out, not_24_out, not_25_out, not_26_out, not_27_out,
       not_28_out, not_29_out, not_30_out, not_31_out, not_32_out, not_33_out, not_34_out, not_35_out,
       not_36_out, not_37_out, not_38_out, not_39_out, not_40_out, not_41_out, not_42_out, not_43_out,
       not_44_out, not_45_out, not_46_out, not_47_out, not_48_out, not_49_out, not_50_out, not_51_out,
       not_52_out, not_53_out, not_54_out, not_55_out, not_56_out, not_57_out, not_58_out, not_59_out,
       not_60_out, not_61_out, not_62_out, not_63_out, not_64_out, not_65_out, not_66_out, not_67_out,
       not_68_out, not_69_out, not_70_out, not_71_out, not_72_out, not_73_out, not_74_out, not_75_out,
       not_76_out, not_77_out, not_78_out, not_79_out, not_80_out, not_81_out, not_82_out, not_83_out,
       not_84_out, not_85_out, not_86_out, not_87_out, not_88_out, not_89_out, not_90_out, not_91_out,
       not_92_out, not_93_out, not_94_out, not_95_out, not_96_out, not_97_out, not_98_out, not_99_out,
       not_100_out, not_101_out, not_102_out, not_103_out, not_104_out, not_105_out, not_106_out,
       not_107_out, not_108_out, not_109_out, not_110_out, not_111_out, not_112_out, not_113_out,
       not_114_out, not_115_out, not_116_out, not_117_out, not_118_out, not_119_out, not_120_out,
       not_121_out, not_122_out, not_123_out, not_124_out, not_125_out, not_126_out, not_127_out,
       not_128_out, not_129_out, not_130_out, not_131_out, not_132_out, not_133_out, not_134_out,
       not_135_out, not_136_out, not_137_out, not_138_out, not_139_out, not_140_out, not_141_out,
       not_142_out, not_143_out, not_144_out, not_145_out, not_146_out, not_147_out, not_148_out,
       not_149_out, not_150_out, not_151_out, not_152_out, not_153_out, not_154_out, not_155_out,
       not_156_out, not_157_out, not_158_out, not_159_out, not_160_out, not_161_out, not_162_out,
       not_163_out, not_164_out, not_165_out, not_166_out, not_167_out, not_168_out, not_169_out,
       not_170_out, not_171_out, not_172_out, not_173_out, not_174_out, not_175_out, not_176_out,
       not_177_out, not_178_out, not_179_out, not_180_out, not_181_out, not_182_out, not_183_out,
       not_184_out, not_185_out, not_186_out, not_187_out, not_188_out, not_189_out, not_190_out,
       not_191_out, not_192_out, not_193_out, not_194_out, not_195_out, not_196_out, not_197_out,
       not_198_out, not_199_out, not_200_out, not_201_out, not_202_out, not_203_out, not_204_out,
       not_205_out, not_206_out, not_207_out, not_208_out, not_209_out, not_210_out, not_211_out,
       not_212_out, not_213_out, not_214_out, not_215_out, not_216_out, not_217_out, not_218_out,
       not_219_out, not_220_out, not_221_out, not_222_out, not_223_out, not_224_out, not_225_out,
       not_226_out, not_227_out, not_228_out, not_229_out, not_230_out, not_231_out, not_232_out,
       not_233_out, not_234_out, not_235_out, not_236_out, not_237_out, not_238_out, not_239_out,
       not_240_out, not_241_out, not_242_out, not_243_out, not_244_out, not_245_out, not_246_out,
       not_247_out, not_248_out, not_249_out, not_250_out, not_251_out, not_252_out, not_253_out,
       not_254_out, not_255_out, not_256_out, not_257_out, not_258_out, not_259_out, not_260_out,
       not_261_out, not_262_out, not_263_out, not_264_out, not_265_out, not_266_out, not_267_out,
       not_268_out, not_269_out, not_270_out, not_271_out, not_272_out, not_273_out, not_274_out,
       not_275_out, not_276_out, not_277_out, not_278_out, not_279_out, not_280_out, not_281_out,
       not_282_out, not_283_out, not_284_out, not_285_out, not_286_out, not_287_out, not_288_out,
       not_289_out, not_290_out, not_291_out, not_292_out, not_293_out, not_294_out, not_295_out,
       not_296_out, not_297_out, not_298_out, not_299_out, not_300_out, not_301_out, not_302_out,
       not_303_out, not_304_out, not_305_out, not_306_out, not_307_out, not_308_out, not_309_out,
       not_310_out, not_311_out, not_312_out, not_313_out, not_314_out, not_315_out, not_316_out,
       not_317_out, not_318_out, not_319_out, not_320_out, not_321_out, not_322_out, not_323_out,
       not_324_out, not_325_out, not_326_out, not_327_out, not_328_out, not_329_out, not_330_out,
       not_331_out, not_332_out, not_333_out, not_334_out, not_335_out, not_336_out, not_337_out,
       not_338_out, not_339_out, not_340_out, not_341_out, not_342_out, not_343_out, not_344_out,
       not_345_out, not_346_out, not_347_out, not_348_out, not_349_out, not_350_out, not_351_out,
       not_352_out, not_353_out, not_354_out, not_355_out, not_356_out, not_357_out, not_358_out,
       not_359_out, not_360_out, not_361_out, not_362_out, not_363_out, not_364_out, not_365_out,
       not_366_out, not_367_out, not_368_out, not_369_out, not_370_out, not_371_out, not_372_out,
       not_373_out, not_374_out, not_375_out, not_376_out, not_377_out, not_378_out, not_379_out,
       not_380_out, not_381_out, not_382_out, not_383_out, not_384_out, not_385_out, not_386_out,
       not_387_out, not_388_out, not_389_out, not_390_out, not_391_out, not_392_out, not_393_out,
       not_394_out, not_395_out, not_396_out, not_397_out, not_398_out, not_399_out, or_1_out, or_2_out,
       or_3_out, or_4_out;

  not not_1 (not_1_out, Opcode[5]);
  not not_2 (not_2_out, Opcode[4]);
  not not_3 (not_3_out, Opcode[3]);
  not not_4 (not_4_out, Opcode[2]);
  not not_5 (not_5_out, Opcode[1]);
  not not_6 (not_6_out, Opcode[0]);
  not not_7 (not_7_out, Funct[4]);
  not not_8 (not_8_out, Funct[3]);
  not not_9 (not_9_out, Funct[2]);
  not not_10 (not_10_out, Funct[1]);
  not not_11 (not_11_out, Funct[0]);
  not not_12 (not_12_out, Opcode[5]);
  not not_13 (not_13_out, Opcode[4]);
  not not_14 (not_14_out, Opcode[3]);
  not not_15 (not_15_out, Opcode[2]);
  not not_16 (not_16_out, Opcode[1]);
  not not_17 (not_17_out, Opcode[0]);
  not not_18 (not_18_out, Funct[4]);
  not not_19 (not_19_out, Funct[3]);
  not not_20 (not_20_out, Funct[2]);
  not not_21 (not_21_out, Funct[0]);
  not not_22 (not_22_out, Opcode[5]);
  not not_23 (not_23_out, Opcode[4]);
  not not_24 (not_24_out, Opcode[3]);
  not not_25 (not_25_out, Opcode[2]);
  not not_26 (not_26_out, Opcode[1]);
  not not_27 (not_27_out, Opcode[0]);
  not not_28 (not_28_out, Funct[4]);
  not not_29 (not_29_out, Funct[3]);
  not not_30 (not_30_out, Funct[1]);
  not not_31 (not_31_out, Funct[0]);
  not not_32 (not_32_out, Opcode[5]);
  not not_33 (not_33_out, Opcode[4]);
  not not_34 (not_34_out, Opcode[3]);
  not not_35 (not_35_out, Opcode[2]);
  not not_36 (not_36_out, Opcode[1]);
  not not_37 (not_37_out, Opcode[0]);
  not not_38 (not_38_out, Funct[4]);
  not not_39 (not_39_out, Funct[3]);
  not not_40 (not_40_out, Opcode[5]);
  not not_41 (not_41_out, Opcode[4]);
  not not_42 (not_42_out, Opcode[3]);
  not not_43 (not_43_out, Opcode[2]);
  not not_44 (not_44_out, Opcode[1]);
  not not_45 (not_45_out, Opcode[0]);
  not not_46 (not_46_out, Funct[5]);
  not not_47 (not_47_out, Funct[4]);
  not not_48 (not_48_out, Funct[3]);
  not not_49 (not_49_out, Funct[2]);
  not not_50 (not_50_out, Funct[1]);
  not not_51 (not_51_out, Funct[0]);
  not not_52 (not_52_out, Opcode[5]);
  not not_53 (not_53_out, Opcode[4]);
  not not_54 (not_54_out, Opcode[3]);
  not not_55 (not_55_out, Opcode[2]);
  not not_56 (not_56_out, Opcode[1]);
  not not_57 (not_57_out, Opcode[0]);
  not not_58 (not_58_out, Funct[5]);
  not not_59 (not_59_out, Funct[4]);
  not not_60 (not_60_out, Funct[3]);
  not not_61 (not_61_out, Funct[2]);
  not not_62 (not_62_out, Funct[0]);
  not not_63 (not_63_out, Opcode[5]);
  not not_64 (not_64_out, Opcode[4]);
  not not_65 (not_65_out, Opcode[3]);
  not not_66 (not_66_out, Opcode[2]);
  not not_67 (not_67_out, Opcode[1]);
  not not_68 (not_68_out, Opcode[0]);
  not not_69 (not_69_out, Funct[4]);
  not not_70 (not_70_out, Funct[3]);
  not not_71 (not_71_out, Funct[2]);
  not not_72 (not_72_out, Funct[1]);
  not not_73 (not_73_out, Funct[0]);
  not not_74 (not_74_out, Opcode[5]);
  not not_75 (not_75_out, Opcode[4]);
  not not_76 (not_76_out, Opcode[3]);
  not not_77 (not_77_out, Opcode[2]);
  not not_78 (not_78_out, Opcode[1]);
  not not_79 (not_79_out, Opcode[0]);
  not not_80 (not_80_out, Funct[4]);
  not not_81 (not_81_out, Funct[3]);
  not not_82 (not_82_out, Funct[2]);
  not not_83 (not_83_out, Funct[0]);
  not not_84 (not_84_out, Opcode[5]);
  not not_85 (not_85_out, Opcode[4]);
  not not_86 (not_86_out, Opcode[3]);
  not not_87 (not_87_out, Opcode[2]);
  not not_88 (not_88_out, Opcode[1]);
  not not_89 (not_89_out, Opcode[0]);
  not not_90 (not_90_out, Funct[4]);
  not not_91 (not_91_out, Funct[2]);
  not not_92 (not_92_out, Funct[0]);
  not not_93 (not_93_out, Opcode[5]);
  not not_94 (not_94_out, Opcode[4]);
  not not_95 (not_95_out, Opcode[3]);
  not not_96 (not_96_out, Opcode[2]);
  not not_97 (not_97_out, Opcode[1]);
  not not_98 (not_98_out, Opcode[0]);
  not not_99 (not_99_out, Funct[5]);
  not not_100 (not_100_out, Funct[4]);
  not not_101 (not_101_out, Funct[3]);
  not not_102 (not_102_out, Funct[2]);
  not not_103 (not_103_out, Funct[1]);
  not not_104 (not_104_out, Funct[0]);
  not not_105 (not_105_out, Opcode[5]);
  not not_106 (not_106_out, Opcode[4]);
  not not_107 (not_107_out, Opcode[3]);
  not not_108 (not_108_out, Opcode[2]);
  not not_109 (not_109_out, Opcode[1]);
  not not_110 (not_110_out, Opcode[0]);
  not not_111 (not_111_out, Funct[5]);
  not not_112 (not_112_out, Funct[4]);
  not not_113 (not_113_out, Funct[3]);
  not not_114 (not_114_out, Funct[2]);
  not not_115 (not_115_out, Funct[0]);
  not not_116 (not_116_out, Opcode[5]);
  not not_117 (not_117_out, Opcode[4]);
  not not_118 (not_118_out, Opcode[3]);
  not not_119 (not_119_out, Opcode[2]);
  not not_120 (not_120_out, Opcode[1]);
  not not_121 (not_121_out, Opcode[0]);
  not not_122 (not_122_out, Funct[4]);
  not not_123 (not_123_out, Funct[3]);
  not not_124 (not_124_out, Funct[2]);
  not not_125 (not_125_out, Funct[1]);
  not not_126 (not_126_out, Funct[0]);
  not not_127 (not_127_out, Opcode[5]);
  not not_128 (not_128_out, Opcode[4]);
  not not_129 (not_129_out, Opcode[3]);
  not not_130 (not_130_out, Opcode[2]);
  not not_131 (not_131_out, Opcode[1]);
  not not_132 (not_132_out, Opcode[0]);
  not not_133 (not_133_out, Funct[4]);
  not not_134 (not_134_out, Funct[3]);
  not not_135 (not_135_out, Funct[1]);
  not not_136 (not_136_out, Funct[0]);
  not not_137 (not_137_out, Opcode[5]);
  not not_138 (not_138_out, Opcode[4]);
  not not_139 (not_139_out, Opcode[3]);
  not not_140 (not_140_out, Opcode[2]);
  not not_141 (not_141_out, Opcode[1]);
  not not_142 (not_142_out, Opcode[0]);
  not not_143 (not_143_out, Funct[4]);
  not not_144 (not_144_out, Funct[3]);
  not not_145 (not_145_out, Funct[1]);
  not not_146 (not_146_out, Opcode[5]);
  not not_147 (not_147_out, Opcode[4]);
  not not_148 (not_148_out, Opcode[3]);
  not not_149 (not_149_out, Opcode[2]);
  not not_150 (not_150_out, Opcode[1]);
  not not_151 (not_151_out, Opcode[0]);
  not not_152 (not_152_out, Funct[5]);
  not not_153 (not_153_out, Funct[4]);
  not not_154 (not_154_out, Funct[3]);
  not not_155 (not_155_out, Funct[2]);
  not not_156 (not_156_out, Funct[1]);
  not not_157 (not_157_out, Funct[0]);
  not not_158 (not_158_out, Opcode[5]);
  not not_159 (not_159_out, Opcode[4]);
  not not_160 (not_160_out, Opcode[3]);
  not not_161 (not_161_out, Opcode[2]);
  not not_162 (not_162_out, Opcode[1]);
  not not_163 (not_163_out, Opcode[0]);
  not not_164 (not_164_out, Funct[4]);
  not not_165 (not_165_out, Funct[3]);
  not not_166 (not_166_out, Funct[2]);
  not not_167 (not_167_out, Funct[1]);
  not not_168 (not_168_out, Funct[0]);
  not not_169 (not_169_out, Opcode[5]);
  not not_170 (not_170_out, Opcode[4]);
  not not_171 (not_171_out, Opcode[3]);
  not not_172 (not_172_out, Opcode[2]);
  not not_173 (not_173_out, Opcode[1]);
  not not_174 (not_174_out, Opcode[0]);
  not not_175 (not_175_out, Funct[4]);
  not not_176 (not_176_out, Funct[3]);
  not not_177 (not_177_out, Funct[2]);
  not not_178 (not_178_out, Funct[0]);
  not not_179 (not_179_out, Opcode[5]);
  not not_180 (not_180_out, Opcode[4]);
  not not_181 (not_181_out, Opcode[3]);
  not not_182 (not_182_out, Opcode[2]);
  not not_183 (not_183_out, Opcode[1]);
  not not_184 (not_184_out, Opcode[0]);
  not not_185 (not_185_out, Funct[4]);
  not not_186 (not_186_out, Funct[3]);
  not not_187 (not_187_out, Funct[1]);
  not not_188 (not_188_out, Funct[0]);
  not not_189 (not_189_out, Opcode[5]);
  not not_190 (not_190_out, Opcode[4]);
  not not_191 (not_191_out, Opcode[3]);
  not not_192 (not_192_out, Opcode[2]);
  not not_193 (not_193_out, Opcode[1]);
  not not_194 (not_194_out, Opcode[0]);
  not not_195 (not_195_out, Funct[4]);
  not not_196 (not_196_out, Funct[3]);
  not not_197 (not_197_out, Funct[1]);
  not not_198 (not_198_out, Opcode[5]);
  not not_199 (not_199_out, Opcode[4]);
  not not_200 (not_200_out, Opcode[3]);
  not not_201 (not_201_out, Opcode[2]);
  not not_202 (not_202_out, Opcode[1]);
  not not_203 (not_203_out, Opcode[0]);
  not not_204 (not_204_out, Funct[4]);
  not not_205 (not_205_out, Funct[2]);
  not not_206 (not_206_out, Funct[0]);
  not not_207 (not_207_out, Opcode[4]);
  not not_208 (not_208_out, Opcode[3]);
  not not_209 (not_209_out, Opcode[2]);
  not not_210 (not_210_out, Opcode[5]);
  not not_211 (not_211_out, Opcode[4]);
  not not_212 (not_212_out, Opcode[2]);
  not not_213 (not_213_out, Opcode[5]);
  not not_214 (not_214_out, Opcode[4]);
  not not_215 (not_215_out, Opcode[3]);
  not not_216 (not_216_out, Opcode[1]);
  not not_217 (not_217_out, Opcode[0]);
  not not_218 (not_218_out, Opcode[5]);
  not not_219 (not_219_out, Opcode[4]);
  not not_220 (not_220_out, Opcode[2]);
  not not_221 (not_221_out, Opcode[1]);
  not not_222 (not_222_out, Opcode[0]);
  not not_223 (not_223_out, Opcode[5]);
  not not_224 (not_224_out, Opcode[4]);
  not not_225 (not_225_out, Opcode[1]);
  not not_226 (not_226_out, Opcode[0]);
  not not_227 (not_227_out, Opcode[5]);
  not not_228 (not_228_out, Opcode[4]);
  not not_229 (not_229_out, Opcode[3]);
  not not_230 (not_230_out, Opcode[2]);
  not not_231 (not_231_out, Opcode[1]);
  not not_232 (not_232_out, Opcode[0]);
  not not_233 (not_233_out, Funct[4]);
  not not_234 (not_234_out, Funct[2]);
  not not_235 (not_235_out, Funct[0]);
  not not_236 (not_236_out, Opcode[5]);
  not not_237 (not_237_out, Opcode[4]);
  not not_238 (not_238_out, Opcode[3]);
  not not_239 (not_239_out, Opcode[2]);
  not not_240 (not_240_out, Opcode[1]);
  not not_241 (not_241_out, Opcode[0]);
  not not_242 (not_242_out, Funct[4]);
  not not_243 (not_243_out, Funct[3]);
  not not_244 (not_244_out, Funct[1]);
  not not_245 (not_245_out, Opcode[5]);
  not not_246 (not_246_out, Opcode[4]);
  not not_247 (not_247_out, Opcode[3]);
  not not_248 (not_248_out, Opcode[2]);
  not not_249 (not_249_out, Opcode[1]);
  not not_250 (not_250_out, Opcode[0]);
  not not_251 (not_251_out, Funct[4]);
  not not_252 (not_252_out, Funct[3]);
  not not_253 (not_253_out, Funct[1]);
  not not_254 (not_254_out, Funct[0]);
  not not_255 (not_255_out, Opcode[5]);
  not not_256 (not_256_out, Opcode[4]);
  not not_257 (not_257_out, Opcode[3]);
  not not_258 (not_258_out, Opcode[2]);
  not not_259 (not_259_out, Opcode[1]);
  not not_260 (not_260_out, Opcode[0]);
  not not_261 (not_261_out, Funct[4]);
  not not_262 (not_262_out, Funct[3]);
  not not_263 (not_263_out, Funct[1]);
  not not_264 (not_264_out, Opcode[5]);
  not not_265 (not_265_out, Opcode[4]);
  not not_266 (not_266_out, Opcode[3]);
  not not_267 (not_267_out, Opcode[2]);
  not not_268 (not_268_out, Opcode[1]);
  not not_269 (not_269_out, Opcode[0]);
  not not_270 (not_270_out, Funct[4]);
  not not_271 (not_271_out, Funct[3]);
  not not_272 (not_272_out, Opcode[5]);
  not not_273 (not_273_out, Opcode[4]);
  not not_274 (not_274_out, Opcode[1]);
  not not_275 (not_275_out, Opcode[0]);
  not not_276 (not_276_out, Opcode[4]);
  not not_277 (not_277_out, Opcode[3]);
  not not_278 (not_278_out, Opcode[2]);
  not not_279 (not_279_out, Opcode[4]);
  not not_280 (not_280_out, Opcode[2]);
  not not_281 (not_281_out, Opcode[5]);
  not not_282 (not_282_out, Opcode[4]);
  not not_283 (not_283_out, Opcode[3]);
  not not_284 (not_284_out, Opcode[1]);
  not not_285 (not_285_out, Opcode[0]);
  not not_286 (not_286_out, Opcode[5]);
  not not_287 (not_287_out, Opcode[4]);
  not not_288 (not_288_out, Opcode[2]);
  not not_289 (not_289_out, Opcode[1]);
  not not_290 (not_290_out, Opcode[0]);
  not not_291 (not_291_out, Opcode[4]);
  not not_292 (not_292_out, Opcode[3]);
  not not_293 (not_293_out, Opcode[2]);
  not not_294 (not_294_out, Opcode[5]);
  not not_295 (not_295_out, Opcode[4]);
  not not_296 (not_296_out, Opcode[2]);
  not not_297 (not_297_out, Opcode[5]);
  not not_298 (not_298_out, Opcode[4]);
  not not_299 (not_299_out, Opcode[2]);
  not not_300 (not_300_out, Opcode[1]);
  not not_301 (not_301_out, Opcode[0]);
  not not_302 (not_302_out, Opcode[5]);
  not not_303 (not_303_out, Opcode[4]);
  not not_304 (not_304_out, Opcode[1]);
  not not_305 (not_305_out, Opcode[0]);
  not not_306 (not_306_out, Opcode[5]);
  not not_307 (not_307_out, Opcode[4]);
  not not_308 (not_308_out, Opcode[3]);
  not not_309 (not_309_out, Opcode[2]);
  not not_310 (not_310_out, Opcode[1]);
  not not_311 (not_311_out, Opcode[0]);
  not not_312 (not_312_out, Funct[4]);
  not not_313 (not_313_out, Funct[3]);
  not not_314 (not_314_out, Funct[2]);
  not not_315 (not_315_out, Funct[0]);
  not not_316 (not_316_out, Opcode[5]);
  not not_317 (not_317_out, Opcode[4]);
  not not_318 (not_318_out, Opcode[3]);
  not not_319 (not_319_out, Opcode[2]);
  not not_320 (not_320_out, Opcode[1]);
  not not_321 (not_321_out, Opcode[0]);
  not not_322 (not_322_out, Funct[4]);
  not not_323 (not_323_out, Funct[3]);
  not not_324 (not_324_out, Opcode[5]);
  not not_325 (not_325_out, Opcode[4]);
  not not_326 (not_326_out, Opcode[3]);
  not not_327 (not_327_out, Opcode[1]);
  not not_328 (not_328_out, Opcode[0]);
  not not_329 (not_329_out, Opcode[5]);
  not not_330 (not_330_out, Opcode[4]);
  not not_331 (not_331_out, Opcode[3]);
  not not_332 (not_332_out, Opcode[2]);
  not not_333 (not_333_out, Opcode[1]);
  not not_334 (not_334_out, Opcode[0]);
  not not_335 (not_335_out, Funct[4]);
  not not_336 (not_336_out, Funct[2]);
  not not_337 (not_337_out, Funct[0]);
  not not_338 (not_338_out, Opcode[5]);
  not not_339 (not_339_out, Opcode[4]);
  not not_340 (not_340_out, Opcode[3]);
  not not_341 (not_341_out, Opcode[2]);
  not not_342 (not_342_out, Opcode[1]);
  not not_343 (not_343_out, Opcode[0]);
  not not_344 (not_344_out, Funct[5]);
  not not_345 (not_345_out, Funct[4]);
  not not_346 (not_346_out, Funct[3]);
  not not_347 (not_347_out, Funct[2]);
  not not_348 (not_348_out, Funct[0]);
  not not_349 (not_349_out, Opcode[4]);
  not not_350 (not_350_out, Opcode[3]);
  not not_351 (not_351_out, Opcode[2]);
  not not_352 (not_352_out, Opcode[5]);
  not not_353 (not_353_out, Opcode[4]);
  not not_354 (not_354_out, Opcode[2]);
  not not_355 (not_355_out, Opcode[5]);
  not not_356 (not_356_out, Opcode[4]);
  not not_357 (not_357_out, Opcode[3]);
  not not_358 (not_358_out, Opcode[1]);
  not not_359 (not_359_out, Opcode[0]);
  not not_360 (not_360_out, Opcode[5]);
  not not_361 (not_361_out, Opcode[4]);
  not not_362 (not_362_out, Opcode[2]);
  not not_363 (not_363_out, Opcode[1]);
  not not_364 (not_364_out, Opcode[0]);
  not not_365 (not_365_out, Opcode[5]);
  not not_366 (not_366_out, Opcode[4]);
  not not_367 (not_367_out, Opcode[1]);
  not not_368 (not_368_out, Opcode[0]);
  not not_369 (not_369_out, Opcode[5]);
  not not_370 (not_370_out, Opcode[4]);
  not not_371 (not_371_out, Opcode[3]);
  not not_372 (not_372_out, Opcode[2]);
  not not_373 (not_373_out, Opcode[1]);
  not not_374 (not_374_out, Opcode[0]);
  not not_375 (not_375_out, Funct[4]);
  not not_376 (not_376_out, Funct[3]);
  not not_377 (not_377_out, Opcode[5]);
  not not_378 (not_378_out, Opcode[4]);
  not not_379 (not_379_out, Opcode[3]);
  not not_380 (not_380_out, Opcode[2]);
  not not_381 (not_381_out, Opcode[1]);
  not not_382 (not_382_out, Opcode[0]);
  not not_383 (not_383_out, Funct[5]);
  not not_384 (not_384_out, Funct[4]);
  not not_385 (not_385_out, Funct[3]);
  not not_386 (not_386_out, Funct[2]);
  not not_387 (not_387_out, Funct[1]);
  not not_388 (not_388_out, Funct[0]);
  not not_389 (not_389_out, Opcode[5]);
  not not_390 (not_390_out, Opcode[4]);
  not not_391 (not_391_out, Opcode[3]);
  not not_392 (not_392_out, Opcode[2]);
  not not_393 (not_393_out, Opcode[1]);
  not not_394 (not_394_out, Opcode[0]);
  not not_395 (not_395_out, Funct[5]);
  not not_396 (not_396_out, Funct[4]);
  not not_397 (not_397_out, Funct[3]);
  not not_398 (not_398_out, Funct[2]);
  not not_399 (not_399_out, Funct[0]);
  and and_1 (and_1_out, not_1_out, not_2_out, not_3_out, not_4_out, not_5_out, not_6_out, Funct[5], not_7_out, not_8_out, not_9_out, not_10_out, not_11_out);
  and and_2 (and_2_out, not_12_out, not_13_out, not_14_out, not_15_out, not_16_out, not_17_out, Funct[5], not_18_out, not_19_out, not_20_out, Funct[1], not_21_out);
  and and_3 (and_3_out, Opcode[5], not_207_out, not_208_out, not_209_out, Opcode[1], Opcode[0]);
  and and_4 (and_4_out, not_210_out, not_211_out, Opcode[3], not_212_out, Opcode[1], Opcode[0]);
  and and_5 (and_5_out, not_22_out, not_23_out, not_24_out, not_25_out, not_26_out, not_27_out, Funct[5], not_28_out, not_29_out, Funct[2], not_30_out, not_31_out);
  and and_6 (and_6_out, not_213_out, not_214_out, not_215_out, Opcode[2], not_216_out, not_217_out);
  and and_7 (and_7_out, not_32_out, not_33_out, not_34_out, not_35_out, not_36_out, not_37_out, Funct[5], not_38_out, not_39_out, Funct[2], Funct[1], Funct[0]);
  and and_8 (and_8_out, not_218_out, not_219_out, Opcode[3], not_220_out, not_221_out, not_222_out);
  and and_9 (and_9_out, not_223_out, not_224_out, Opcode[3], Opcode[2], not_225_out, not_226_out);
  and and_10 (and_10_out, not_40_out, not_41_out, not_42_out, not_43_out, not_44_out, not_45_out, not_46_out, not_47_out, not_48_out, not_49_out, not_50_out, not_51_out);
  and and_11 (and_11_out, not_52_out, not_53_out, not_54_out, not_55_out, not_56_out, not_57_out, not_58_out, not_59_out, not_60_out, not_61_out, Funct[1], not_62_out);
  and and_12 (and_12_out, not_245_out, not_246_out, not_247_out, not_248_out, not_249_out, not_250_out, Funct[5], not_251_out, not_252_out, Funct[2], not_253_out, not_254_out);
  and and_13 (and_13_out, not_255_out, not_256_out, not_257_out, not_258_out, not_259_out, not_260_out, Funct[5], not_261_out, not_262_out, Funct[2], not_263_out, Funct[0]);
  and and_14 (and_14_out, not_264_out, not_265_out, not_266_out, not_267_out, not_268_out, not_269_out, Funct[5], not_270_out, not_271_out, Funct[2], Funct[1], Funct[0]);
  and and_15 (and_15_out, not_272_out, not_273_out, Opcode[3], Opcode[2], not_274_out, not_275_out);
  and and_16 (and_16_out, not_63_out, not_64_out, not_65_out, not_66_out, not_67_out, not_68_out, Funct[5], not_69_out, not_70_out, not_71_out, not_72_out, not_73_out);
  and and_17 (and_17_out, not_74_out, not_75_out, not_76_out, not_77_out, not_78_out, not_79_out, Funct[5], not_80_out, not_81_out, not_82_out, Funct[1], not_83_out);
  and and_18 (and_18_out, Opcode[5], not_276_out, not_277_out, not_278_out, Opcode[1], Opcode[0]);
  and and_19 (and_19_out, Opcode[5], not_279_out, Opcode[3], not_280_out, Opcode[1], Opcode[0]);
  and and_20 (and_20_out, not_281_out, not_282_out, not_283_out, Opcode[2], not_284_out, not_285_out);
  and and_21 (and_21_out, not_84_out, not_85_out, not_86_out, not_87_out, not_88_out, not_89_out, Funct[5], not_90_out, Funct[3], not_91_out, Funct[1], not_92_out);
  and and_22 (and_22_out, not_286_out, not_287_out, Opcode[3], not_288_out, not_289_out, not_290_out);
  and and_23 (and_23_out, not_93_out, not_94_out, not_95_out, not_96_out, not_97_out, not_98_out, not_99_out, not_100_out, not_101_out, not_102_out, not_103_out, not_104_out);
  and and_24 (and_24_out, not_105_out, not_106_out, not_107_out, not_108_out, not_109_out, not_110_out, not_111_out, not_112_out, not_113_out, not_114_out, Funct[1], not_115_out);
  and and_25 (and_25_out, not_116_out, not_117_out, not_118_out, not_119_out, not_120_out, not_121_out, Funct[5], not_122_out, not_123_out, not_124_out, not_125_out, not_126_out);
  and and_26 (and_26_out, Opcode[5], not_291_out, not_292_out, not_293_out, Opcode[1], Opcode[0]);
  and and_27 (and_27_out, not_294_out, not_295_out, Opcode[3], not_296_out, Opcode[1], Opcode[0]);
  and and_28 (and_28_out, not_127_out, not_128_out, not_129_out, not_130_out, not_131_out, not_132_out, Funct[5], not_133_out, not_134_out, Funct[2], not_135_out, not_136_out);
  and and_29 (and_29_out, not_137_out, not_138_out, not_139_out, not_140_out, not_141_out, not_142_out, Funct[5], not_143_out, not_144_out, Funct[2], not_145_out, Funct[0]);
  and and_30 (and_30_out, not_297_out, not_298_out, Opcode[3], not_299_out, not_300_out, not_301_out);
  and and_31 (and_31_out, not_302_out, not_303_out, Opcode[3], Opcode[2], not_304_out, not_305_out);
  and and_32 (and_32_out, not_146_out, not_147_out, not_148_out, not_149_out, not_150_out, not_151_out, not_152_out, not_153_out, not_154_out, not_155_out, not_156_out, not_157_out);
  and and_33 (and_33_out, not_306_out, not_307_out, not_308_out, not_309_out, not_310_out, not_311_out, Funct[5], not_312_out, not_313_out, not_314_out, Funct[1], not_315_out);
  and and_34 (and_34_out, not_316_out, not_317_out, not_318_out, not_319_out, not_320_out, not_321_out, Funct[5], not_322_out, not_323_out, Funct[2], Funct[1], Funct[0]);
  and and_35 (and_35_out, not_324_out, not_325_out, not_326_out, Opcode[2], not_327_out, not_328_out);
  and and_36 (and_36_out, not_329_out, not_330_out, not_331_out, not_332_out, not_333_out, not_334_out, Funct[5], not_335_out, Funct[3], not_336_out, Funct[1], not_337_out);
  and and_37 (and_37_out, not_338_out, not_339_out, not_340_out, not_341_out, not_342_out, not_343_out, not_344_out, not_345_out, not_346_out, not_347_out, Funct[1], not_348_out);
  and and_38 (and_38_out, not_158_out, not_159_out, not_160_out, not_161_out, not_162_out, not_163_out, Funct[5], not_164_out, not_165_out, not_166_out, not_167_out, not_168_out);
  and and_39 (and_39_out, not_169_out, not_170_out, not_171_out, not_172_out, not_173_out, not_174_out, Funct[5], not_175_out, not_176_out, not_177_out, Funct[1], not_178_out);
  and and_40 (and_40_out, Opcode[5], not_349_out, not_350_out, not_351_out, Opcode[1], Opcode[0]);
  and and_41 (and_41_out, not_352_out, not_353_out, Opcode[3], not_354_out, Opcode[1], Opcode[0]);
  and and_42 (and_42_out, not_179_out, not_180_out, not_181_out, not_182_out, not_183_out, not_184_out, Funct[5], not_185_out, not_186_out, Funct[2], not_187_out, not_188_out);
  and and_43 (and_43_out, not_189_out, not_190_out, not_191_out, not_192_out, not_193_out, not_194_out, Funct[5], not_195_out, not_196_out, Funct[2], not_197_out, Funct[0]);
  and and_44 (and_44_out, not_355_out, not_356_out, not_357_out, Opcode[2], not_358_out, not_359_out);
  and and_45 (and_45_out, not_198_out, not_199_out, not_200_out, not_201_out, not_202_out, not_203_out, Funct[5], not_204_out, Funct[3], not_205_out, Funct[1], not_206_out);
  and and_46 (and_46_out, not_360_out, not_361_out, Opcode[3], not_362_out, not_363_out, not_364_out);
  and and_47 (and_47_out, not_365_out, not_366_out, Opcode[3], Opcode[2], not_367_out, not_368_out);
  nor nor_1 (nor_1_out, and_1_out, and_2_out, and_3_out, and_4_out, and_5_out, and_6_out, and_7_out, and_8_out, and_9_out, and_10_out, and_11_out);
  and and_48 (and_48_out, not_227_out, not_228_out, not_229_out, not_230_out, not_231_out, not_232_out, Funct[5], not_233_out, Funct[3], not_234_out, Funct[1], not_235_out);
  or or_1 (or_1_out, and_48_out, and_49_out);
  and and_49 (and_49_out, not_236_out, not_237_out, not_238_out, not_239_out, not_240_out, not_241_out, Funct[5], not_242_out, not_243_out, Funct[2], not_244_out, Funct[0]);
  nor nor_2 (nor_2_out, and_12_out, and_13_out, and_14_out, and_15_out);
  or or_2 (or_2_out, and_16_out, and_17_out, and_18_out, and_19_out, and_20_out, and_21_out, and_22_out, and_23_out, and_24_out);
  nor nor_3 (nor_3_out, and_25_out, and_26_out, and_27_out, and_28_out, and_29_out, and_30_out, and_31_out, and_32_out);
  or or_3 (or_3_out, and_33_out, and_34_out, and_35_out, and_36_out, and_37_out);
  nor nor_4 (nor_4_out, and_38_out, and_39_out, and_40_out, and_41_out, and_42_out, and_43_out, and_44_out, and_45_out, and_46_out, and_47_out);
  and and_50 (and_50_out, not_369_out, not_370_out, not_371_out, not_372_out, not_373_out, not_374_out, Funct[5], not_375_out, not_376_out, Funct[2], Funct[1], Funct[0]);
  or or_4 (or_4_out, and_50_out, and_51_out, and_52_out);
  and and_51 (and_51_out, not_377_out, not_378_out, not_379_out, not_380_out, not_381_out, not_382_out, not_383_out, not_384_out, not_385_out, not_386_out, not_387_out, not_388_out);
  and and_52 (and_52_out, not_389_out, not_390_out, not_391_out, not_392_out, not_393_out, not_394_out, not_395_out, not_396_out, not_397_out, not_398_out, Funct[1], not_399_out);
  and and_53 (ALUCtl[0], nor_1_out, or_1_out);
  and and_54 (ALUCtl[1], nor_2_out, or_2_out);
  and and_55 (ALUCtl[2], nor_3_out, or_3_out);
  and and_56 (ALUCtl[3], nor_4_out, or_4_out);

  // Other names for the same wires on the sheet: o0 = ALUCtl[0]; o1 = ALUCtl[1]; o2 = ALUCtl[2]; o3 = ALUCtl[3]
endmodule

module ControlUnit (
  input  [5:0] Opcode,
  input  Clock,
  output PCWriteCond,
  output PCWrite,
  output IRWrite,
  output ALUSrcA,
  output IORD,
  output [1:0] PCSource,
  output [1:0] ALUSrcB,
  output RegDST,
  output MemtoReg,
  output MemRead,
  output MemWrite,
  output RegWrite
);

  wire and_1_out, comparator_1_gt, not_1_out, opdecode_1_i, opdecode_1_r;
  wire [3:0] rom_1_data;
  wire [6:4] rom_2_data;
  wire [8:0] opdecode_1_j;

  OPDecode opdecode_1 (
    .Op0(Opcode[0]), .Op1(Opcode[1]), .Op2(Opcode[2]), .Op3(Opcode[3]), .Op4(Opcode[4]), .Op5(Opcode[5]),
    .LW(opdecode_1_j[4]), .SW(opdecode_1_j[3]), .R(opdecode_1_r), .BEQ(opdecode_1_j[1]), .J(opdecode_1_j[0]),
    .I(opdecode_1_i));
  or or_1 (opdecode_1_j[2], opdecode_1_r, opdecode_1_i);
  ROM #(.addrWidth(9), .dataWidth(4)) rom_1 (.addr(opdecode_1_j), .data(rom_1_data), .sel(1'b1));
  Register #(.width(4)) register_1 (.D(rom_1_data), .Q(opdecode_1_j[8:5]), .clk(Clock));  // open: en, clr
  ROM #(.addrWidth(4), .dataWidth(14)) rom_2 (
    .addr(opdecode_1_j[8:5]),
    .data({PCWriteCond, PCWrite, IRWrite, ALUSrcA, IORD, PCSource, rom_2_data, MemtoReg, MemRead, MemWrite, RegWrite}),
    .sel(1'b1));
  not not_1 (not_1_out, opdecode_1_i);
  Multiplexer #(.enable("false")) multiplexer_1 (
    .in0(rom_2_data[4]), .in1(not_1_out), .out(RegDST), .sel(opdecode_1_i));
  and and_1 (and_1_out, opdecode_1_i, comparator_1_gt);
  Multiplexer #(.width(2), .enable("false")) multiplexer_2 (
    .in0(rom_2_data[6:5]), .in1(2'b10), .out(ALUSrcB), .sel(and_1_out));
  Comparator #(.width(4), .mode("unsigned")) comparator_1 (
    .a(opdecode_1_j[8:5]), .b(4'b0000), .gt(comparator_1_gt));  // open: eq, lt

  // Notes on the sheet:
  //   contents of rom_1 (hex, n*v repeats v):
  //   32*1 0 9 8 0 6 0 0 0 2 7*0 2 7*0 2 15*0 5 7*0 3 15*0 32*4 64*0 32*7
  //   contents of rom_2 (hex, n*v repeats v):
  //   1824 60 440 204 9 202 400 11 2480 1100
endmodule

module OPDecode (
  input  Op0,
  input  Op1,
  input  Op2,
  input  Op3,
  input  Op4,
  input  Op5,
  output LW,
  output SW,
  output R,
  output BEQ,
  output J,
  output I
);

  wire and_6_out, and_7_out, and_8_out, not_1_out, not_2_out, not_3_out, not_4_out, not_5_out, not_6_out,
       not_7_out, not_8_out, not_9_out, not_10_out, not_11_out, not_12_out, not_13_out, not_14_out,
       not_15_out, not_16_out, not_17_out, not_18_out, not_19_out, not_20_out, not_21_out, not_22_out,
       not_23_out, not_24_out, not_25_out, not_26_out, not_27_out, not_28_out, not_29_out, not_30_out,
       not_31_out, not_32_out, not_33_out;

  not not_1 (not_1_out, Op4);
  not not_2 (not_2_out, Op3);
  not not_3 (not_3_out, Op2);
  not not_4 (not_4_out, Op4);
  not not_5 (not_5_out, Op2);
  not not_6 (not_6_out, Op5);
  not not_7 (not_7_out, Op4);
  not not_8 (not_8_out, Op3);
  not not_9 (not_9_out, Op2);
  not not_10 (not_10_out, Op1);
  not not_11 (not_11_out, Op0);
  not not_12 (not_12_out, Op5);
  not not_13 (not_13_out, Op4);
  not not_14 (not_14_out, Op3);
  not not_15 (not_15_out, Op1);
  not not_16 (not_16_out, Op0);
  not not_17 (not_17_out, Op5);
  not not_18 (not_18_out, Op4);
  not not_19 (not_19_out, Op3);
  not not_20 (not_20_out, Op2);
  not not_21 (not_21_out, Op0);
  not not_22 (not_22_out, Op5);
  not not_23 (not_23_out, Op4);
  not not_24 (not_24_out, Op1);
  not not_25 (not_25_out, Op0);
  not not_26 (not_26_out, Op5);
  not not_27 (not_27_out, Op4);
  not not_28 (not_28_out, Op2);
  not not_29 (not_29_out, Op1);
  not not_30 (not_30_out, Op0);
  not not_31 (not_31_out, Op5);
  not not_32 (not_32_out, Op4);
  not not_33 (not_33_out, Op1);
  and and_1 (LW, Op5, not_1_out, not_2_out, not_3_out, Op1, Op0);
  and and_2 (SW, Op5, not_4_out, Op3, not_5_out, Op1, Op0);
  and and_3 (R, not_6_out, not_7_out, not_8_out, not_9_out, not_10_out, not_11_out);
  and and_4 (BEQ, not_12_out, not_13_out, not_14_out, Op2, not_15_out, not_16_out);
  and and_5 (J, not_17_out, not_18_out, not_19_out, not_20_out, Op1, not_21_out);
  and and_6 (and_6_out, not_22_out, not_23_out, Op3, Op2, not_24_out, not_25_out);
  and and_7 (and_7_out, not_26_out, not_27_out, Op3, not_28_out, not_29_out, not_30_out);
  and and_8 (and_8_out, not_31_out, not_32_out, Op3, Op2, not_33_out, Op0);
  or or_1 (I, and_6_out, and_7_out, and_8_out);
endmodule

module ALUControlNew (
  input  i0,
  input  i1,
  input  i2,
  input  i3,
  input  i4,
  input  i5,
  input  i26,
  input  i27,
  input  i28,
  input  i29,
  input  i30,
  input  i31,
  output o0,
  output o1,
  output o2,
  output o3
);

  wire and_1_out, and_2_out, and_3_out, and_4_out, and_5_out, and_6_out, and_7_out, and_8_out, and_9_out,
       and_10_out, and_11_out, and_12_out, and_13_out, and_14_out, and_15_out, and_16_out, and_17_out,
       and_18_out, and_19_out, and_20_out, and_21_out, and_22_out, and_23_out, and_24_out, and_25_out,
       and_26_out, and_27_out, and_28_out, and_29_out, and_30_out, and_31_out, and_32_out, and_33_out,
       and_34_out, and_35_out, and_36_out, and_37_out, and_38_out, and_39_out, and_40_out, and_41_out,
       and_42_out, and_43_out, and_44_out, and_45_out, and_46_out, and_47_out, and_48_out, and_49_out,
       and_50_out, and_51_out, and_52_out, and_53_out, and_54_out, and_55_out, nor_1_out, nor_2_out,
       nor_3_out, nor_4_out, not_1_out, not_2_out, not_3_out, not_4_out, not_5_out, not_6_out, not_7_out,
       not_8_out, not_9_out, not_10_out, not_11_out, not_12_out, not_13_out, not_14_out, not_15_out,
       not_16_out, not_17_out, not_18_out, not_19_out, not_20_out, not_21_out, not_22_out, not_23_out,
       not_24_out, not_25_out, not_26_out, not_27_out, not_28_out, not_29_out, not_30_out, not_31_out,
       not_32_out, not_33_out, not_34_out, not_35_out, not_36_out, not_37_out, not_38_out, not_39_out,
       not_40_out, not_41_out, not_42_out, not_43_out, not_44_out, not_45_out, not_46_out, not_47_out,
       not_48_out, not_49_out, not_50_out, not_51_out, not_52_out, not_53_out, not_54_out, not_55_out,
       not_56_out, not_57_out, not_58_out, not_59_out, not_60_out, not_61_out, not_62_out, not_63_out,
       not_64_out, not_65_out, not_66_out, not_67_out, not_68_out, not_69_out, not_70_out, not_71_out,
       not_72_out, not_73_out, not_74_out, not_75_out, not_76_out, not_77_out, not_78_out, not_79_out,
       not_80_out, not_81_out, not_82_out, not_83_out, not_84_out, not_85_out, not_86_out, not_87_out,
       not_88_out, not_89_out, not_90_out, not_91_out, not_92_out, not_93_out, not_94_out, not_95_out,
       not_96_out, not_97_out, not_98_out, not_99_out, not_100_out, not_101_out, not_102_out, not_103_out,
       not_104_out, not_105_out, not_106_out, not_107_out, not_108_out, not_109_out, not_110_out,
       not_111_out, not_112_out, not_113_out, not_114_out, not_115_out, not_116_out, not_117_out,
       not_118_out, not_119_out, not_120_out, not_121_out, not_122_out, not_123_out, not_124_out,
       not_125_out, not_126_out, not_127_out, not_128_out, not_129_out, not_130_out, not_131_out,
       not_132_out, not_133_out, not_134_out, not_135_out, not_136_out, not_137_out, not_138_out,
       not_139_out, not_140_out, not_141_out, not_142_out, not_143_out, not_144_out, not_145_out,
       not_146_out, not_147_out, not_148_out, not_149_out, not_150_out, not_151_out, not_152_out,
       not_153_out, not_154_out, not_155_out, not_156_out, not_157_out, not_158_out, not_159_out,
       not_160_out, not_161_out, not_162_out, not_163_out, not_164_out, not_165_out, not_166_out,
       not_167_out, not_168_out, not_169_out, not_170_out, not_171_out, not_172_out, not_173_out,
       not_174_out, not_175_out, not_176_out, not_177_out, not_178_out, not_179_out, not_180_out,
       not_181_out, not_182_out, not_183_out, not_184_out, not_185_out, not_186_out, not_187_out,
       not_188_out, not_189_out, not_190_out, not_191_out, not_192_out, not_193_out, not_194_out,
       not_195_out, not_196_out, not_197_out, not_198_out, not_199_out, not_200_out, not_201_out,
       not_202_out, not_203_out, not_204_out, not_205_out, not_206_out, not_207_out, not_208_out,
       not_209_out, not_210_out, not_211_out, not_212_out, not_213_out, not_214_out, not_215_out,
       not_216_out, not_217_out, not_218_out, not_219_out, not_220_out, not_221_out, not_222_out,
       not_223_out, not_224_out, not_225_out, not_226_out, not_227_out, not_228_out, not_229_out,
       not_230_out, not_231_out, not_232_out, not_233_out, not_234_out, not_235_out, not_236_out,
       not_237_out, not_238_out, not_239_out, not_240_out, not_241_out, not_242_out, not_243_out,
       not_244_out, not_245_out, not_246_out, not_247_out, not_248_out, not_249_out, not_250_out,
       not_251_out, not_252_out, not_253_out, not_254_out, not_255_out, not_256_out, not_257_out,
       not_258_out, not_259_out, not_260_out, not_261_out, not_262_out, not_263_out, not_264_out,
       not_265_out, not_266_out, not_267_out, not_268_out, not_269_out, not_270_out, not_271_out,
       not_272_out, not_273_out, not_274_out, not_275_out, not_276_out, not_277_out, not_278_out,
       not_279_out, not_280_out, not_281_out, not_282_out, not_283_out, not_284_out, not_285_out,
       not_286_out, not_287_out, not_288_out, not_289_out, not_290_out, not_291_out, not_292_out,
       not_293_out, not_294_out, not_295_out, not_296_out, not_297_out, not_298_out, not_299_out,
       not_300_out, not_301_out, not_302_out, not_303_out, not_304_out, not_305_out, not_306_out,
       not_307_out, not_308_out, not_309_out, not_310_out, not_311_out, not_312_out, not_313_out,
       not_314_out, not_315_out, not_316_out, not_317_out, not_318_out, not_319_out, not_320_out,
       not_321_out, not_322_out, not_323_out, not_324_out, not_325_out, not_326_out, not_327_out,
       not_328_out, not_329_out, not_330_out, not_331_out, not_332_out, not_333_out, not_334_out,
       not_335_out, not_336_out, not_337_out, not_338_out, not_339_out, not_340_out, not_341_out,
       not_342_out, not_343_out, not_344_out, not_345_out, not_346_out, not_347_out, not_348_out,
       not_349_out, not_350_out, not_351_out, not_352_out, not_353_out, not_354_out, not_355_out,
       not_356_out, not_357_out, not_358_out, not_359_out, not_360_out, not_361_out, not_362_out,
       not_363_out, not_364_out, not_365_out, not_366_out, not_367_out, not_368_out, not_369_out,
       not_370_out, not_371_out, not_372_out, not_373_out, not_374_out, not_375_out, not_376_out,
       not_377_out, not_378_out, not_379_out, not_380_out, not_381_out, not_382_out, not_383_out,
       not_384_out, not_385_out, not_386_out, not_387_out, not_388_out, not_389_out, not_390_out,
       not_391_out, not_392_out, not_393_out, not_394_out, not_395_out, not_396_out, not_397_out,
       not_398_out, or_1_out, or_2_out, or_3_out, or_4_out;

  not not_1 (not_1_out, i31);
  not not_2 (not_2_out, i30);
  not not_3 (not_3_out, i29);
  not not_4 (not_4_out, i28);
  not not_5 (not_5_out, i27);
  not not_6 (not_6_out, i26);
  not not_7 (not_7_out, i4);
  not not_8 (not_8_out, i3);
  not not_9 (not_9_out, i1);
  not not_10 (not_10_out, i31);
  not not_11 (not_11_out, i30);
  not not_12 (not_12_out, i29);
  not not_13 (not_13_out, i28);
  not not_14 (not_14_out, i27);
  not not_15 (not_15_out, i26);
  not not_16 (not_16_out, i4);
  not not_17 (not_17_out, i2);
  not not_18 (not_18_out, i0);
  not not_19 (not_19_out, i31);
  not not_20 (not_20_out, i30);
  not not_21 (not_21_out, i29);
  not not_22 (not_22_out, i28);
  not not_23 (not_23_out, i27);
  not not_24 (not_24_out, i26);
  not not_25 (not_25_out, i5);
  not not_26 (not_26_out, i4);
  not not_27 (not_27_out, i3);
  not not_28 (not_28_out, i2);
  not not_29 (not_29_out, i0);
  not not_30 (not_30_out, i31);
  not not_31 (not_31_out, i30);
  not not_32 (not_32_out, i29);
  not not_33 (not_33_out, i28);
  not not_34 (not_34_out, i27);
  not not_35 (not_35_out, i26);
  not not_36 (not_36_out, i5);
  not not_37 (not_37_out, i4);
  not not_38 (not_38_out, i3);
  not not_39 (not_39_out, i2);
  not not_40 (not_40_out, i1);
  not not_41 (not_41_out, i0);
  not not_42 (not_42_out, i31);
  not not_43 (not_43_out, i30);
  not not_44 (not_44_out, i29);
  not not_45 (not_45_out, i28);
  not not_46 (not_46_out, i27);
  not not_47 (not_47_out, i26);
  not not_48 (not_48_out, i4);
  not not_49 (not_49_out, i3);
  not not_50 (not_50_out, i2);
  not not_51 (not_51_out, i1);
  not not_52 (not_52_out, i0);
  not not_53 (not_53_out, i31);
  not not_54 (not_54_out, i30);
  not not_55 (not_55_out, i28);
  not not_56 (not_56_out, i27);
  not not_57 (not_57_out, i26);
  not not_58 (not_58_out, i31);
  not not_59 (not_59_out, i30);
  not not_60 (not_60_out, i29);
  not not_61 (not_61_out, i28);
  not not_62 (not_62_out, i27);
  not not_63 (not_63_out, i26);
  not not_64 (not_64_out, i4);
  not not_65 (not_65_out, i3);
  not not_66 (not_66_out, i2);
  not not_67 (not_67_out, i0);
  not not_68 (not_68_out, i30);
  not not_69 (not_69_out, i29);
  not not_70 (not_70_out, i28);
  not not_71 (not_71_out, i30);
  not not_72 (not_72_out, i28);
  not not_73 (not_73_out, i31);
  not not_74 (not_74_out, i30);
  not not_75 (not_75_out, i29);
  not not_76 (not_76_out, i28);
  not not_77 (not_77_out, i27);
  not not_78 (not_78_out, i26);
  not not_79 (not_79_out, i4);
  not not_80 (not_80_out, i3);
  not not_81 (not_81_out, i1);
  not not_82 (not_82_out, i0);
  not not_83 (not_83_out, i31);
  not not_84 (not_84_out, i30);
  not not_85 (not_85_out, i29);
  not not_86 (not_86_out, i28);
  not not_87 (not_87_out, i27);
  not not_88 (not_88_out, i26);
  not not_89 (not_89_out, i4);
  not not_90 (not_90_out, i3);
  not not_91 (not_91_out, i31);
  not not_92 (not_92_out, i30);
  not not_93 (not_93_out, i27);
  not not_94 (not_94_out, i26);
  not not_95 (not_95_out, i31);
  not not_96 (not_96_out, i30);
  not not_97 (not_97_out, i29);
  not not_98 (not_98_out, i27);
  not not_99 (not_99_out, i26);
  not not_100 (not_100_out, i31);
  not not_101 (not_101_out, i30);
  not not_102 (not_102_out, i29);
  not not_103 (not_103_out, i28);
  not not_104 (not_104_out, i27);
  not not_105 (not_105_out, i26);
  not not_106 (not_106_out, i5);
  not not_107 (not_107_out, i4);
  not not_108 (not_108_out, i3);
  not not_109 (not_109_out, i2);
  not not_110 (not_110_out, i0);
  not not_111 (not_111_out, i31);
  not not_112 (not_112_out, i30);
  not not_113 (not_113_out, i29);
  not not_114 (not_114_out, i28);
  not not_115 (not_115_out, i27);
  not not_116 (not_116_out, i26);
  not not_117 (not_117_out, i5);
  not not_118 (not_118_out, i4);
  not not_119 (not_119_out, i3);
  not not_120 (not_120_out, i2);
  not not_121 (not_121_out, i1);
  not not_122 (not_122_out, i0);
  not not_123 (not_123_out, i31);
  not not_124 (not_124_out, i30);
  not not_125 (not_125_out, i29);
  not not_126 (not_126_out, i28);
  not not_127 (not_127_out, i27);
  not not_128 (not_128_out, i26);
  not not_129 (not_129_out, i4);
  not not_130 (not_130_out, i3);
  not not_131 (not_131_out, i2);
  not not_132 (not_132_out, i1);
  not not_133 (not_133_out, i0);
  not not_134 (not_134_out, i31);
  not not_135 (not_135_out, i30);
  not not_136 (not_136_out, i28);
  not not_137 (not_137_out, i27);
  not not_138 (not_138_out, i26);
  not not_139 (not_139_out, i31);
  not not_140 (not_140_out, i30);
  not not_141 (not_141_out, i29);
  not not_142 (not_142_out, i28);
  not not_143 (not_143_out, i27);
  not not_144 (not_144_out, i26);
  not not_145 (not_145_out, i4);
  not not_146 (not_146_out, i3);
  not not_147 (not_147_out, i2);
  not not_148 (not_148_out, i0);
  not not_149 (not_149_out, i30);
  not not_150 (not_150_out, i29);
  not not_151 (not_151_out, i28);
  not not_152 (not_152_out, i30);
  not not_153 (not_153_out, i28);
  not not_154 (not_154_out, i31);
  not not_155 (not_155_out, i30);
  not not_156 (not_156_out, i29);
  not not_157 (not_157_out, i27);
  not not_158 (not_158_out, i26);
  not not_159 (not_159_out, i31);
  not not_160 (not_160_out, i30);
  not not_161 (not_161_out, i29);
  not not_162 (not_162_out, i28);
  not not_163 (not_163_out, i27);
  not not_164 (not_164_out, i26);
  not not_165 (not_165_out, i4);
  not not_166 (not_166_out, i2);
  not not_167 (not_167_out, i0);
  not not_168 (not_168_out, i31);
  not not_169 (not_169_out, i30);
  not not_170 (not_170_out, i29);
  not not_171 (not_171_out, i28);
  not not_172 (not_172_out, i27);
  not not_173 (not_173_out, i26);
  not not_174 (not_174_out, i4);
  not not_175 (not_175_out, i3);
  not not_176 (not_176_out, i1);
  not not_177 (not_177_out, i0);
  not not_178 (not_178_out, i31);
  not not_179 (not_179_out, i30);
  not not_180 (not_180_out, i29);
  not not_181 (not_181_out, i28);
  not not_182 (not_182_out, i27);
  not not_183 (not_183_out, i26);
  not not_184 (not_184_out, i4);
  not not_185 (not_185_out, i3);
  not not_186 (not_186_out, i1);
  not not_187 (not_187_out, i31);
  not not_188 (not_188_out, i30);
  not not_189 (not_189_out, i29);
  not not_190 (not_190_out, i28);
  not not_191 (not_191_out, i27);
  not not_192 (not_192_out, i26);
  not not_193 (not_193_out, i4);
  not not_194 (not_194_out, i3);
  not not_195 (not_195_out, i31);
  not not_196 (not_196_out, i30);
  not not_197 (not_197_out, i27);
  not not_198 (not_198_out, i26);
  not not_199 (not_199_out, i31);
  not not_200 (not_200_out, i30);
  not not_201 (not_201_out, i27);
  not not_202 (not_202_out, i31);
  not not_203 (not_203_out, i30);
  not not_204 (not_204_out, i29);
  not not_205 (not_205_out, i28);
  not not_206 (not_206_out, i27);
  not not_207 (not_207_out, i26);
  not not_208 (not_208_out, i5);
  not not_209 (not_209_out, i4);
  not not_210 (not_210_out, i3);
  not not_211 (not_211_out, i2);
  not not_212 (not_212_out, i0);
  not not_213 (not_213_out, i31);
  not not_214 (not_214_out, i30);
  not not_215 (not_215_out, i29);
  not not_216 (not_216_out, i28);
  not not_217 (not_217_out, i27);
  not not_218 (not_218_out, i26);
  not not_219 (not_219_out, i4);
  not not_220 (not_220_out, i3);
  not not_221 (not_221_out, i2);
  not not_222 (not_222_out, i0);
  not not_223 (not_223_out, i31);
  not not_224 (not_224_out, i30);
  not not_225 (not_225_out, i29);
  not not_226 (not_226_out, i28);
  not not_227 (not_227_out, i27);
  not not_228 (not_228_out, i26);
  not not_229 (not_229_out, i4);
  not not_230 (not_230_out, i3);
  not not_231 (not_231_out, i31);
  not not_232 (not_232_out, i30);
  not not_233 (not_233_out, i29);
  not not_234 (not_234_out, i27);
  not not_235 (not_235_out, i26);
  not not_236 (not_236_out, i31);
  not not_237 (not_237_out, i30);
  not not_238 (not_238_out, i29);
  not not_239 (not_239_out, i28);
  not not_240 (not_240_out, i27);
  not not_241 (not_241_out, i26);
  not not_242 (not_242_out, i4);
  not not_243 (not_243_out, i2);
  not not_244 (not_244_out, i0);
  not not_245 (not_245_out, i31);
  not not_246 (not_246_out, i30);
  not not_247 (not_247_out, i29);
  not not_248 (not_248_out, i28);
  not not_249 (not_249_out, i27);
  not not_250 (not_250_out, i26);
  not not_251 (not_251_out, i5);
  not not_252 (not_252_out, i4);
  not not_253 (not_253_out, i3);
  not not_254 (not_254_out, i2);
  not not_255 (not_255_out, i1);
  not not_256 (not_256_out, i0);
  not not_257 (not_257_out, i31);
  not not_258 (not_258_out, i30);
  not not_259 (not_259_out, i29);
  not not_260 (not_260_out, i28);
  not not_261 (not_261_out, i27);
  not not_262 (not_262_out, i26);
  not not_263 (not_263_out, i4);
  not not_264 (not_264_out, i3);
  not not_265 (not_265_out, i2);
  not not_266 (not_266_out, i1);
  not not_267 (not_267_out, i0);
  not not_268 (not_268_out, i31);
  not not_269 (not_269_out, i30);
  not not_270 (not_270_out, i28);
  not not_271 (not_271_out, i27);
  not not_272 (not_272_out, i26);
  not not_273 (not_273_out, i30);
  not not_274 (not_274_out, i29);
  not not_275 (not_275_out, i28);
  not not_276 (not_276_out, i30);
  not not_277 (not_277_out, i28);
  not not_278 (not_278_out, i31);
  not not_279 (not_279_out, i30);
  not not_280 (not_280_out, i29);
  not not_281 (not_281_out, i28);
  not not_282 (not_282_out, i27);
  not not_283 (not_283_out, i26);
  not not_284 (not_284_out, i4);
  not not_285 (not_285_out, i3);
  not not_286 (not_286_out, i1);
  not not_287 (not_287_out, i0);
  not not_288 (not_288_out, i31);
  not not_289 (not_289_out, i30);
  not not_290 (not_290_out, i29);
  not not_291 (not_291_out, i28);
  not not_292 (not_292_out, i27);
  not not_293 (not_293_out, i26);
  not not_294 (not_294_out, i4);
  not not_295 (not_295_out, i3);
  not not_296 (not_296_out, i1);
  not not_297 (not_297_out, i31);
  not not_298 (not_298_out, i30);
  not not_299 (not_299_out, i27);
  not not_300 (not_300_out, i26);
  not not_301 (not_301_out, i31);
  not not_302 (not_302_out, i30);
  not not_303 (not_303_out, i27);
  not not_304 (not_304_out, i31);
  not not_305 (not_305_out, i30);
  not not_306 (not_306_out, i29);
  not not_307 (not_307_out, i28);
  not not_308 (not_308_out, i27);
  not not_309 (not_309_out, i26);
  not not_310 (not_310_out, i4);
  not not_311 (not_311_out, i3);
  not not_312 (not_312_out, i31);
  not not_313 (not_313_out, i30);
  not not_314 (not_314_out, i29);
  not not_315 (not_315_out, i28);
  not not_316 (not_316_out, i27);
  not not_317 (not_317_out, i26);
  not not_318 (not_318_out, i5);
  not not_319 (not_319_out, i4);
  not not_320 (not_320_out, i3);
  not not_321 (not_321_out, i2);
  not not_322 (not_322_out, i1);
  not not_323 (not_323_out, i0);
  not not_324 (not_324_out, i31);
  not not_325 (not_325_out, i30);
  not not_326 (not_326_out, i29);
  not not_327 (not_327_out, i28);
  not not_328 (not_328_out, i27);
  not not_329 (not_329_out, i26);
  not not_330 (not_330_out, i5);
  not not_331 (not_331_out, i4);
  not not_332 (not_332_out, i3);
  not not_333 (not_333_out, i2);
  not not_334 (not_334_out, i0);
  not not_335 (not_335_out, i31);
  not not_336 (not_336_out, i30);
  not not_337 (not_337_out, i29);
  not not_338 (not_338_out, i28);
  not not_339 (not_339_out, i27);
  not not_340 (not_340_out, i26);
  not not_341 (not_341_out, i4);
  not not_342 (not_342_out, i3);
  not not_343 (not_343_out, i2);
  not not_344 (not_344_out, i1);
  not not_345 (not_345_out, i0);
  not not_346 (not_346_out, i31);
  not not_347 (not_347_out, i30);
  not not_348 (not_348_out, i28);
  not not_349 (not_349_out, i27);
  not not_350 (not_350_out, i26);
  not not_351 (not_351_out, i30);
  not not_352 (not_352_out, i29);
  not not_353 (not_353_out, i28);
  not not_354 (not_354_out, i30);
  not not_355 (not_355_out, i28);
  not not_356 (not_356_out, i31);
  not not_357 (not_357_out, i30);
  not not_358 (not_358_out, i29);
  not not_359 (not_359_out, i28);
  not not_360 (not_360_out, i27);
  not not_361 (not_361_out, i26);
  not not_362 (not_362_out, i4);
  not not_363 (not_363_out, i3);
  not not_364 (not_364_out, i1);
  not not_365 (not_365_out, i0);
  not not_366 (not_366_out, i31);
  not not_367 (not_367_out, i30);
  not not_368 (not_368_out, i29);
  not not_369 (not_369_out, i28);
  not not_370 (not_370_out, i27);
  not not_371 (not_371_out, i26);
  not not_372 (not_372_out, i4);
  not not_373 (not_373_out, i3);
  not not_374 (not_374_out, i1);
  not not_375 (not_375_out, i31);
  not not_376 (not_376_out, i30);
  not not_377 (not_377_out, i27);
  not not_378 (not_378_out, i26);
  not not_379 (not_379_out, i31);
  not not_380 (not_380_out, i30);
  not not_381 (not_381_out, i27);
  not not_382 (not_382_out, i31);
  not not_383 (not_383_out, i30);
  not not_384 (not_384_out, i29);
  not not_385 (not_385_out, i27);
  not not_386 (not_386_out, i26);
  not not_387 (not_387_out, i31);
  not not_388 (not_388_out, i30);
  not not_389 (not_389_out, i29);
  not not_390 (not_390_out, i28);
  not not_391 (not_391_out, i27);
  not not_392 (not_392_out, i26);
  not not_393 (not_393_out, i4);
  not not_394 (not_394_out, i2);
  not not_395 (not_395_out, i0);
  not not_396 (not_396_out, i31);
  not not_397 (not_397_out, i30);
  not not_398 (not_398_out, i27);
  and and_1 (and_1_out, not_19_out, not_20_out, not_21_out, not_22_out, not_23_out, not_24_out, not_25_out, not_26_out, not_27_out, not_28_out, i1, not_29_out);
  and and_2 (and_2_out, not_30_out, not_31_out, not_32_out, not_33_out, not_34_out, not_35_out, not_36_out, not_37_out, not_38_out, not_39_out, not_40_out, not_41_out);
  and and_3 (and_3_out, not_42_out, not_43_out, not_44_out, not_45_out, not_46_out, not_47_out, i5, not_48_out, not_49_out, not_50_out, not_51_out, not_52_out);
  and and_4 (and_4_out, not_53_out, not_54_out, i29, not_55_out, not_56_out, not_57_out);
  and and_5 (and_5_out, not_58_out, not_59_out, not_60_out, not_61_out, not_62_out, not_63_out, i5, not_64_out, not_65_out, not_66_out, i1, not_67_out);
  and and_6 (and_6_out, i31, not_68_out, not_69_out, not_70_out, i27, i26);
  and and_7 (and_7_out, i31, not_71_out, i29, not_72_out, i27, i26);
  and and_8 (and_8_out, not_73_out, not_74_out, not_75_out, not_76_out, not_77_out, not_78_out, i5, not_79_out, not_80_out, i2, not_81_out, not_82_out);
  and and_9 (and_9_out, not_83_out, not_84_out, not_85_out, not_86_out, not_87_out, not_88_out, i5, not_89_out, not_90_out, i2, i1, i0);
  and and_10 (and_10_out, not_91_out, not_92_out, i29, i28, not_93_out, not_94_out);
  and and_11 (and_11_out, not_95_out, not_96_out, not_97_out, i28, not_98_out, not_99_out);
  and and_12 (and_12_out, not_100_out, not_101_out, not_102_out, not_103_out, not_104_out, not_105_out, not_106_out, not_107_out, not_108_out, not_109_out, i1, not_110_out);
  and and_13 (and_13_out, not_111_out, not_112_out, not_113_out, not_114_out, not_115_out, not_116_out, not_117_out, not_118_out, not_119_out, not_120_out, not_121_out, not_122_out);
  and and_14 (and_14_out, not_123_out, not_124_out, not_125_out, not_126_out, not_127_out, not_128_out, i5, not_129_out, not_130_out, not_131_out, not_132_out, not_133_out);
  and and_15 (and_15_out, not_134_out, not_135_out, i29, not_136_out, not_137_out, not_138_out);
  and and_16 (and_16_out, not_139_out, not_140_out, not_141_out, not_142_out, not_143_out, not_144_out, i5, not_145_out, not_146_out, not_147_out, i1, not_148_out);
  and and_17 (and_17_out, i31, not_149_out, not_150_out, not_151_out, i27, i26);
  and and_18 (and_18_out, i31, not_152_out, i29, not_153_out, i27, i26);
  and and_19 (and_19_out, not_154_out, not_155_out, not_156_out, i28, not_157_out, not_158_out);
  and and_20 (and_20_out, not_159_out, not_160_out, not_161_out, not_162_out, not_163_out, not_164_out, i5, not_165_out, i3, not_166_out, i1, not_167_out);
  and and_21 (and_21_out, not_168_out, not_169_out, not_170_out, not_171_out, not_172_out, not_173_out, i5, not_174_out, not_175_out, i2, not_176_out, not_177_out);
  and and_22 (and_22_out, not_178_out, not_179_out, not_180_out, not_181_out, not_182_out, not_183_out, i5, not_184_out, not_185_out, i2, not_186_out, i0);
  and and_23 (and_23_out, not_187_out, not_188_out, not_189_out, not_190_out, not_191_out, not_192_out, i5, not_193_out, not_194_out, i2, i1, i0);
  and and_24 (and_24_out, not_195_out, not_196_out, i29, i28, not_197_out, not_198_out);
  and and_25 (and_25_out, not_199_out, not_200_out, i29, i28, not_201_out, i26);
  and and_26 (and_26_out, not_202_out, not_203_out, not_204_out, not_205_out, not_206_out, not_207_out, not_208_out, not_209_out, not_210_out, not_211_out, i1, not_212_out);
  and and_27 (and_27_out, not_213_out, not_214_out, not_215_out, not_216_out, not_217_out, not_218_out, i5, not_219_out, not_220_out, not_221_out, i1, not_222_out);
  and and_28 (and_28_out, not_223_out, not_224_out, not_225_out, not_226_out, not_227_out, not_228_out, i5, not_229_out, not_230_out, i2, i1, i0);
  and and_29 (and_29_out, not_231_out, not_232_out, not_233_out, i28, not_234_out, not_235_out);
  and and_30 (and_30_out, not_236_out, not_237_out, not_238_out, not_239_out, not_240_out, not_241_out, i5, not_242_out, i3, not_243_out, i1, not_244_out);
  and and_31 (and_31_out, not_245_out, not_246_out, not_247_out, not_248_out, not_249_out, not_250_out, not_251_out, not_252_out, not_253_out, not_254_out, not_255_out, not_256_out);
  and and_32 (and_32_out, not_257_out, not_258_out, not_259_out, not_260_out, not_261_out, not_262_out, i5, not_263_out, not_264_out, not_265_out, not_266_out, not_267_out);
  and and_33 (and_33_out, not_268_out, not_269_out, i29, not_270_out, not_271_out, not_272_out);
  and and_34 (and_34_out, i31, not_273_out, not_274_out, not_275_out, i27, i26);
  and and_35 (and_35_out, i31, not_276_out, i29, not_277_out, i27, i26);
  and and_36 (and_36_out, not_278_out, not_279_out, not_280_out, not_281_out, not_282_out, not_283_out, i5, not_284_out, not_285_out, i2, not_286_out, not_287_out);
  and and_37 (and_37_out, not_288_out, not_289_out, not_290_out, not_291_out, not_292_out, not_293_out, i5, not_294_out, not_295_out, i2, not_296_out, i0);
  and and_38 (and_38_out, not_297_out, not_298_out, i29, i28, not_299_out, not_300_out);
  and and_39 (and_39_out, not_301_out, not_302_out, i29, i28, not_303_out, i26);
  and and_40 (and_40_out, not_335_out, not_336_out, not_337_out, not_338_out, not_339_out, not_340_out, i5, not_341_out, not_342_out, not_343_out, not_344_out, not_345_out);
  and and_41 (and_41_out, not_346_out, not_347_out, i29, not_348_out, not_349_out, not_350_out);
  and and_42 (and_42_out, i31, not_351_out, not_352_out, not_353_out, i27, i26);
  and and_43 (and_43_out, i31, not_354_out, i29, not_355_out, i27, i26);
  and and_44 (and_44_out, not_356_out, not_357_out, not_358_out, not_359_out, not_360_out, not_361_out, i5, not_362_out, not_363_out, i2, not_364_out, not_365_out);
  and and_45 (and_45_out, not_366_out, not_367_out, not_368_out, not_369_out, not_370_out, not_371_out, i5, not_372_out, not_373_out, i2, not_374_out, i0);
  and and_46 (and_46_out, not_375_out, not_376_out, i29, i28, not_377_out, not_378_out);
  and and_47 (and_47_out, not_379_out, not_380_out, i29, i28, not_381_out, i26);
  and and_48 (and_48_out, not_382_out, not_383_out, not_384_out, i28, not_385_out, not_386_out);
  and and_49 (and_49_out, not_387_out, not_388_out, not_389_out, not_390_out, not_391_out, not_392_out, i5, not_393_out, i3, not_394_out, i1, not_395_out);
  and and_50 (and_50_out, not_1_out, not_2_out, not_3_out, not_4_out, not_5_out, not_6_out, i5, not_7_out, not_8_out, i2, not_9_out, i0);
  and and_51 (and_51_out, not_396_out, not_397_out, i29, i28, not_398_out, i26);
  and and_52 (and_52_out, not_10_out, not_11_out, not_12_out, not_13_out, not_14_out, not_15_out, i5, not_16_out, i3, not_17_out, i1, not_18_out);
  or or_1 (or_1_out, and_12_out, and_13_out, and_14_out, and_15_out, and_16_out, and_17_out, and_18_out, and_19_out, and_20_out);
  nor nor_1 (nor_1_out, and_21_out, and_22_out, and_23_out, and_24_out, and_25_out);
  or or_2 (or_2_out, and_26_out, and_27_out, and_28_out, and_29_out, and_30_out);
  nor nor_2 (nor_2_out, and_31_out, and_32_out, and_33_out, and_34_out, and_35_out, and_36_out, and_37_out, and_38_out, and_39_out);
  and and_53 (and_53_out, not_304_out, not_305_out, not_306_out, not_307_out, not_308_out, not_309_out, i5, not_310_out, not_311_out, i2, i1, i0);
  and and_54 (and_54_out, not_312_out, not_313_out, not_314_out, not_315_out, not_316_out, not_317_out, not_318_out, not_319_out, not_320_out, not_321_out, not_322_out, not_323_out);
  and and_55 (and_55_out, not_324_out, not_325_out, not_326_out, not_327_out, not_328_out, not_329_out, not_330_out, not_331_out, not_332_out, not_333_out, i1, not_334_out);
  or or_3 (or_3_out, and_50_out, and_51_out, and_52_out);
  and and_56 (o0, or_3_out, nor_3_out);
  nor nor_3 (nor_3_out, and_1_out, and_2_out, and_3_out, and_4_out, and_5_out, and_6_out, and_7_out, and_8_out, and_9_out, and_10_out, and_11_out);
  and and_57 (o1, or_1_out, nor_1_out);
  and and_58 (o2, or_2_out, nor_2_out);
  or or_4 (or_4_out, and_53_out, and_54_out, and_55_out);
  and and_59 (o3, or_4_out, nor_4_out);
  nor nor_4 (nor_4_out, and_40_out, and_41_out, and_42_out, and_43_out, and_44_out, and_45_out, and_46_out, and_47_out, and_48_out, and_49_out);
endmodule
