// Logisim project MultiCycleMips.circ as structural Verilog: 2 circuits, main circuit main
module main (
);

  wire Alu_A_Select, Branch, BranchDestWrite, Clock, IR_Write, Is_Branch, Mem_Address_Select, Mem_Read,
       Mem_Write, or_1_out, PC_Write, WrReg, Zero;
  wire [1:0] Alu_B_Select, Next_PC_Select, Reg2WriteSelect, Write_Data_Select;
  wire [2:0] AluCntrl;
  wire [4:0] Reg2Write;
  wire [7:0] multiplexer_2_out;
  wire [25:0] JumpAddr;
  wire [31:0] ALUA, ALUB, AluResult, BranchAddr, Immediate, Mem, multiplexer_1_out, PC, RegIn, RegValue,
       shifter_1_out, shifter_2_out, ToMem;
  wire [31:26] IR_q;

  Clock clock_1 (.out(Clock));
  Multiplexer #(.select(2), .width(32), .enable("false")) multiplexer_1 (
    .in0(AluResult), .in1(BranchAddr), .in2({PC[31:28], JumpAddr, 2'b00}), .in3(RegValue),
    .out(multiplexer_1_out), .sel(Next_PC_Select));
  or or_1 (or_1_out, PC_Write, Branch);
  and and_1 (Branch, Is_Branch, Zero);
  Register #(.width(32)) u_PC (.D(multiplexer_1_out), .en(or_1_out), .Q(PC), .clk(Clock));  // open: clr
  Multiplexer #(.width(8), .enable("false")) multiplexer_2 (
    .in0(PC[9:2]), .in1(AluResult[7:0]), .out(multiplexer_2_out), .sel(Mem_Address_Select));
  Multiplexer #(.select(2), .width(32), .enable("false")) multiplexer_3 (
    .in0(AluResult), .in1(Mem), .in2(PC), .out(RegIn), .sel(Write_Data_Select));  // open: in3
  RAM #(.dataWidth(32), .bus("separate")) ram_1 (
    .addr(multiplexer_2_out), .din(ToMem), .data(Mem), .str(Mem_Write), .clk(Clock), .ld(Mem_Read));  // open: sel, clr
  Multiplexer #(.select(2), .width(5), .enable("false")) multiplexer_4 (
    .in0(JumpAddr[20:16]), .in1(JumpAddr[15:11]), .in2({5{1'b1}}), .out(Reg2Write), .sel(Reg2WriteSelect));  // open: in3
  Register #(.width(32)) IR (.D(Mem), .en(IR_Write), .Q({IR_q, JumpAddr}), .clk(Clock));  // open: clr
  RegFile regfile_1 (
    .WrAddr(Reg2Write), .WrData(RegIn), .WrReg(WrReg), .RdAddr1(JumpAddr[25:21]), .RdAddr2(JumpAddr[20:16]),
    .RdData1(RegValue), .RdData2(ToMem), .Clock(Clock));
  assign Immediate = {{16{JumpAddr[15]}}, JumpAddr[15:0]};  // Bit_Extender bit_extender_1
  Shifter #(.width(32)) shifter_1 (.in(Immediate), .\dist (5'b00010), .out(shifter_1_out));
  Multiplexer #(.select(2), .width(32), .enable("false")) multiplexer_5 (
    .in0(ToMem), .in1(Immediate), .in2(shifter_1_out), .in3(32'h4), .out(ALUB), .sel(Alu_B_Select));
  Control_Signals control_signals_1 (
    .Instruction({IR_q, JumpAddr}), .PC_Write(PC_Write), .IR_Write(IR_Write),
    .Next_PC_Select(Next_PC_Select), .Is_Branch(Is_Branch), .Branch_Dest_Write(BranchDestWrite),
    .Mem_Read(Mem_Read), .Mem_Write(Mem_Write), .Mem_Address_Select(Mem_Address_Select),
    .ALU_A_Select(Alu_A_Select), .ALU_B_Select(Alu_B_Select), .WrReg(WrReg),
    .Reg_To_Write_Select(Reg2WriteSelect), .WrData_Select(Write_Data_Select), .AluCntrl(AluCntrl),
    .Clock(Clock));
  Multiplexer #(.width(32), .enable("false")) multiplexer_6 (.in0(RegValue), .in1(PC), .out(ALUA), .sel(Alu_A_Select));
  // Probe on AluCntrl
  ALU alu_1 (
    .ALUCtl(AluCntrl), .A(ALUA), .B(ALUB), .ALUResult(AluResult), .Zero(Zero), .Shamt(JumpAddr[10:6]));  // open: Overflow
  Register #(.width(32)) BracnhDest (.D(AluResult), .en(BranchDestWrite), .Q(BranchAddr), .clk(Clock));  // open: clr
  Shifter #(.width(32), .shift("ar")) shifter_2 (.in(PC), .\dist (5'b00010), .out(shifter_2_out));
  // Probe on AluResult
  // Probe on RegIn
  // Probe on shifter_2_out
  // Probe on Next_PC_Select
  // Probe on Branch
  // Probe on WrReg
  // Probe on Reg2Write
  // Probe on Mem_Write
  // Probe on ToMem
  // Probe on Alu_B_Select

  // Other names for the same wires on the sheet: Shamt[4:0] = JumpAddr[10:6]; Rd[4:0] = JumpAddr[15:11];
  //   Rt[4:0] = JumpAddr[20:16]; Rs[4:0] = JumpAddr[25:21]
endmodule

module Control_Signals (
  input  [31:0] Instruction,
  input  Clock,
  output PC_Write,
  output IR_Write,
  output [1:0] Next_PC_Select,
  output Is_Branch,
  output Branch_Dest_Write,
  output Mem_Read,
  output Mem_Write,
  output Mem_Address_Select,
  output ALU_A_Select,
  output [1:0] ALU_B_Select,
  output WrReg,
  output [1:0] Reg_To_Write_Select,
  output [1:0] WrData_Select,
  output [2:0] AluCntrl
);

  wire [2:0] NextState;
  wire [22:0] rom_1_data;

  // Probe on {NextState, Instruction[31], Instruction[29:26], Instruction[5], Instruction[3:0]}
  ROM #(.addrWidth(13), .dataWidth(23)) rom_1 (
    .addr({NextState, Instruction[31], Instruction[29:26], Instruction[5], Instruction[3:0]}),
    .data(rom_1_data));  // open: sel
  Register #(.width(23)) PC (
    .D(rom_1_data),
    .Q({NextState, PC_Write, IR_Write, Next_PC_Select, Is_Branch, Branch_Dest_Write, Mem_Read, Mem_Write, Mem_Address_Select, ALU_A_Select, ALU_B_Select, WrReg, Reg_To_Write_Select, WrData_Select, AluCntrl}),
    .clk(Clock));  // open: en, clr

  // Notes on the sheet:
  //   contents of rom_1 (hex, n*v repeats v):
  //   1024*1c2700 1024*204600 400026 80004 400027 5*80004 b0000 7*80004 400020 80004 400021 80004 400022
  //   400023 80004 400024 80004 80004 400025 5*80004 32*7fffff 32*a0000 32*a00d0 32*18001 96*7fffff
  //   32*400100 96*7fffff 32*400102 32*400103 160*7fffff 32*320900 224*7fffff 32*320900 736*7fffff
  //   32*422900 224*7fffff 32*21900 128*7fffff a6 7fffff a7 13*7fffff a0 7fffff a1 7fffff a2 a3 7fffff a4
  //   7fffff 7fffff a5 229*7fffff 32*180 96*7fffff 32*182 32*183 160*7fffff 32*22988 3456*7fffff
endmodule
