// Logisim project MIPS_Pipelined.circ as structural Verilog: 23 circuits, main circuit main
// ExceptionHandler
module main (
  output IF_Flush,
  output ID_Flush,
  output [31:0] EPC_31__0,
  output EX_Flush,
  output Overflow,
  output [31:0] Cause_31__0
);

  wire ALUSrc, and_1_out, Branch, CLOCK, control_1_alusrc, control_1_i_type, control_1_memread,
       control_1_memtoreg, control_1_regdst, control_1_regwrite, EX_MEM_memtoreg_2, EX_MEM_MemWrite,
       EX_MEM_RegWrite, Exception, FLUSH, id_ex_1_memtoreg_2, id_ex_1_memwrite_2, ID_EX_I_Type,
       ID_EX_MemRead, ID_EX_RegWrite, ID_Zero, IF_ID_MemWrite, Jump, mem_wb_1_memtoreg_2, MEM_WB_RegWrite,
       MEM_WB_Zero, MemRead, not_1_out, not_2_out, RegDst, Stall, SWMux, Zero;
  wire [1:0] BeqFWA, BeqFWB, FWDA, FWDB;
  wire [3:0] ALUCtl, control_1_aluctl;
  wire [4:0] EX_MEM_RegisterRd, EX_SHAmt, id_ex_1_id_ex_rd_out, ID_EX_RegisterRs, ID_EX_RegisterRt, IF_ID_Rd,
       IF_ID_Rs, IF_ID_Rt, MEM_WB_RegisterRd, multiplexer_4_out, SHAmt;
  wire [5:0] Func, OpCode;
  wire [7:0] bit_extender_1_out, bit_extender_4_out;
  wire [15:0] if_id_1_imm;
  wire [25:0] J_Adress;
  wire [27:0] bit_extender_3_out, shifter_2_out;
  wire [31:0] adder_2_out, ALU_A, ALU_B, ALUResult, EX_Immediate, EX_MEM_wrdata, EX_RdData1, EX_RdData2,
       ID_EX_PC_4, if_id_1_pc_4_out, Imm, mem_wb_1_aluout, mem_wb_1_memdataout, MEMALUOut, multiplexer_1_out,
       multiplexer_2_out, multiplexer_5_out, multiplexer_6_out, multiplexer_7_out, multiplexer_10_out, NewPC,
       PC, PC_4, ram_1_data, RdData1, RdData2, rom_1_data, shifter_1_out, WBWriteData;

  // Probe on NewPC
  Multiplexer #(.width(32), .enable("false")) multiplexer_1 (
    .in0(NewPC), .in1(32'h190), .out(multiplexer_1_out), .sel(Exception));
  not not_1 (not_1_out, Stall);
  Clock clock_1 (.out(CLOCK));
  // Probe on multiplexer_1_out
  Register #(.width(32)) register_1 (.D(multiplexer_1_out), .en(not_1_out), .Q(PC), .clk(CLOCK));  // open: clr
  Bit_Extender #(.in_width(32), .out_width(8), .\type ("sign")) bit_extender_1 (.in(PC), .out(bit_extender_1_out));
  Squash squash_1 (
    .Cause(Cause_31__0), .IF_ID(IF_Flush), .ID_EX(ID_Flush), .Flush(FLUSH), .EX_MEM(EX_Flush), .Jump(Jump),
    .MEM_WB(MEM_WB_Zero), .Branch(Branch), .Exception(Exception), .Clock(CLOCK), .Stall(Stall));
  Adder #(.width(32)) adder_1 (.a(PC), .b(32'h4), .out(PC_4));  // open: cin, cout
  ExceptionHandling exceptionhandling_1 (
    .clk(CLOCK), .Overflow(Overflow), .Instr(OpCode), .PC_4(PC_4), .FLUSH(FLUSH), .EPC(EPC_31__0),
    .Cause(Cause_31__0), .Func(Func));
  StallCircuit stallcircuit_1 (
    .IF_ID_MemWrite(IF_ID_MemWrite), .ID_EX_MemRead(ID_EX_MemRead), .ID_EX_Rt(ID_EX_RegisterRt),
    .IF_ID_Rt(IF_ID_Rt), .IF_ID_Rs(IF_ID_Rs), .Branch(Branch), .Stall(Stall), .EX_MEM_MemRead(MemRead),
    .EX_MEM_Rd(EX_MEM_RegisterRd), .ID_EX_RegWrite(ID_EX_RegWrite));
  ForwardUnit forwardunit_1 (
    .ID_EX_RegiterRs(ID_EX_RegisterRs), .EX_Mem_MemWrite(EX_MEM_MemWrite),
    .ID_EX_RegiterRt(ID_EX_RegisterRt), .EX_MEM_RegiterRd(EX_MEM_RegisterRd),
    .MEM_WB_RegiterRd(MEM_WB_RegisterRd), .EX_MEM_RegWrite(EX_MEM_RegWrite),
    .MEM_WB_RegWrite(MEM_WB_RegWrite), .ID_EX_I_Type(ID_EX_I_Type), .ForwardA(FWDA),
    .MEM_WB_ForwardMem(SWMux), .ForwardB(FWDB));
  ROM #(.dataWidth(32)) rom_1 (.addr(bit_extender_1_out), .data(rom_1_data));  // open: sel
  // Probe on IF_ID_Rd
  IF_ID if_id_1 (
    .PC_4_in(PC_4), .in_2(rom_1_data), .Clock(CLOCK), .PC_4_out(if_id_1_pc_4_out), .Imm(if_id_1_imm),
    .Func(Func), .Opcode(OpCode), .Rs(IF_ID_Rs), .Rt(IF_ID_Rt), .Rd(IF_ID_Rd), .SHAmt(SHAmt), .Stall(Stall),
    .Zero(IF_Flush), .J_address(J_Adress));
  assign Imm = {{16{if_id_1_imm[15]}}, if_id_1_imm};  // Bit_Extender bit_extender_2
  // Probe on OpCode
  RegisterFile registerfile_1 (
    .WriteData(WBWriteData), .ReadReg2(IF_ID_Rt), .RegWrite(MEM_WB_RegWrite), .WriteReg(MEM_WB_RegisterRd),
    .Read_Data2(RdData2), .Read_Data1(RdData1), .clock(not_2_out), .Read_Reg1(IF_ID_Rs));
  not not_2 (not_2_out, CLOCK);
  BranchJumpControl branchjumpcontrol_1 (
    .o5(OpCode[5]), .o4(OpCode[4]), .o3(OpCode[3]), .o2(OpCode[2]), .o1(OpCode[1]), .o0(OpCode[0]),
    .branch(Branch), .jump(Jump));
  // Probe on PC_4
  Shifter #(.width(32)) shifter_1 (.in(Imm), .\dist (5'b00010), .out(shifter_1_out));
  assign bit_extender_3_out = {{2{1'b1}}, J_Adress};  // Bit_Extender bit_extender_3
  // Probe on IF_ID_Rt
  // Probe on EX_MEM_RegisterRd
  // Probe on MEM_WB_RegisterRd
  and and_1 (and_1_out, Branch, ID_Zero);
  Adder #(.width(32)) adder_2 (.a(PC), .b(shifter_1_out), .out(adder_2_out));  // open: cin, cout
  Shifter #(.width(28)) shifter_2 (.in(bit_extender_3_out), .\dist (5'b00010), .out(shifter_2_out));
  Control control_1 (
    .FuncBits(Func), .Opcode(OpCode), .ALUCtl(control_1_aluctl), .RegDst(control_1_regdst),
    .ALUSrc(control_1_alusrc), .MemRead(control_1_memread), .MemWrite(IF_ID_MemWrite),
    .RegWrite(control_1_regwrite), .MemToReg(control_1_memtoreg), .I_Type(control_1_i_type));
  BeqForwardNew beqforwardnew_1 (
    .EX_MEM_ReadMem(MemRead), .EX_MEM_RegWrite(EX_MEM_RegWrite), .IF_ID_RegisterRs(IF_ID_Rs),
    .EX_MEM_RegisterRd(EX_MEM_RegisterRd), .IF_ID_RegisterRt(IF_ID_Rt),
    .MEM_WB_RegisterRd(MEM_WB_RegisterRd), .MEM_WB_RegWrite(MEM_WB_RegWrite), .ForwardA(BeqFWA),
    .ForwardB(BeqFWB));
  // Probe on IF_ID_Rs
  Multiplexer #(.width(32), .enable("false")) multiplexer_2 (
    .in0(PC_4), .in1(adder_2_out), .out(multiplexer_2_out), .sel(and_1_out));
  Multiplexer #(.width(32), .enable("false")) multiplexer_3 (
    .in0(multiplexer_2_out), .in1({PC_4[31:28], shifter_2_out}), .out(NewPC), .sel(Jump));
  ID_EX id_ex_1 (
    .ALUCtl(control_1_aluctl), .PC_4_in(if_id_1_pc_4_out), .RegDst(control_1_regdst),
    .ALUSrc(control_1_alusrc), .ReadData1_in(RdData1), .MemRead(control_1_memread),
    .MemWrite(IF_ID_MemWrite), .ReadData2_in(RdData2), .RegWrite(control_1_regwrite),
    .MemToReg(control_1_memtoreg), .Clk(CLOCK), .ExtendedImmediate_in(Imm), .IF_ID_Rt_in(IF_ID_Rt),
    .IF_ID_Rd_in(IF_ID_Rd), .ALUCtl_2(ALUCtl), .PC_4_out(ID_EX_PC_4), .RegDst_2(RegDst), .ALUSrc_2(ALUSrc),
    .ReadData1_out(EX_RdData1), .MemRead_2(ID_EX_MemRead), .MemWrite_2(id_ex_1_memwrite_2),
    .ReadData2_out(EX_RdData2), .RegWrite_2(ID_EX_RegWrite), .MemToReg_2(id_ex_1_memtoreg_2),
    .ExtendedImmediate_out(EX_Immediate), .ID_EX_Rt_out(ID_EX_RegisterRt),
    .ID_EX_Rd_out(id_ex_1_id_ex_rd_out), .SHAmt_in(SHAmt), .SHAmt_out(EX_SHAmt), .IF_ID_Rs_in(IF_ID_Rs),
    .ID_EX_Rs_out(ID_EX_RegisterRs), .I_Type(control_1_i_type), .I_Type_2(ID_EX_I_Type), .Stall(Stall),
    .Zero(ID_Flush));
  Multiplexer #(.width(5), .enable("false")) multiplexer_4 (
    .in0(ID_EX_RegisterRt), .in1(id_ex_1_id_ex_rd_out), .out(multiplexer_4_out), .sel(RegDst));
  // Probe on RdData2
  // Probe on WBWriteData
  // Probe on MEMALUOut
  ALU alu_1 (
    .ALUCtl(ALUCtl), .A(ALU_A), .B(ALU_B), .ALUResult(ALUResult), .Zero(Zero), .SHamt(EX_SHAmt),
    .Overflow(Overflow));
  // Probe on MEMALUOut
  // Probe on WBWriteData
  // Probe on RdData1
  Multiplexer #(.select(2), .width(32), .enable("false")) multiplexer_5 (
    .in0(EX_RdData2), .in1(WBWriteData), .in2(MEMALUOut), .in3(MEMALUOut), .out(multiplexer_5_out), .sel(FWDB));
  // Probe on BeqFWA
  Multiplexer #(.select(2), .width(32), .enable("false")) multiplexer_6 (
    .in0(RdData1), .in1(WBWriteData), .in2(MEMALUOut), .in3(MEMALUOut), .out(multiplexer_6_out), .sel(BeqFWA));
  Multiplexer #(.select(2), .width(32), .enable("false")) multiplexer_7 (
    .in0(RdData2), .in1(WBWriteData), .in2(MEMALUOut), .in3(MEMALUOut), .out(multiplexer_7_out), .sel(BeqFWB));
  // Probe on BeqFWB
  Multiplexer #(.select(2), .width(32), .enable("false")) multiplexer_8 (
    .in0(EX_RdData1), .in1(WBWriteData), .in2(MEMALUOut), .in3(MEMALUOut), .out(ALU_A), .sel(FWDA));
  Multiplexer #(.width(32), .enable("false")) multiplexer_9 (
    .in0(multiplexer_5_out), .in1(EX_Immediate), .out(ALU_B), .sel(ALUSrc));
  Comparator #(.width(32), .mode("unsigned")) comparator_1 (
    .a(multiplexer_6_out), .b(multiplexer_7_out), .eq(ID_Zero));  // open: gt, lt
  // Probe on multiplexer_6_out
  // Probe on multiplexer_7_out
  EX_MEM EX_MEM (
    .MemRead(ID_EX_MemRead), .ALUResult(ALUResult), .MemWrite(id_ex_1_memwrite_2), .RegWrite(ID_EX_RegWrite),
    .RdData2_in(EX_RdData2), .MemToReg(id_ex_1_memtoreg_2), .WrAddr_in(multiplexer_4_out), .Clk(CLOCK),
    .MemRead_2(MemRead), .ALUOut(MEMALUOut), .MemWrite_2(EX_MEM_MemWrite), .RegWrite_2(EX_MEM_RegWrite),
    .WrData(EX_MEM_wrdata), .MemToReg_2(EX_MEM_memtoreg_2), .WrAddr_out(EX_MEM_RegisterRd), .Zero(EX_Flush));
  Multiplexer #(.width(32), .enable("false")) multiplexer_10 (
    .in0(EX_MEM_wrdata), .in1(WBWriteData), .out(multiplexer_10_out), .sel(SWMux));
  Bit_Extender #(.in_width(32), .out_width(8)) bit_extender_4 (.in(MEMALUOut), .out(bit_extender_4_out));
  MEM_WB mem_wb_1 (
    .RegWrite(EX_MEM_RegWrite), .MemDataIn(ram_1_data), .MemToReg(EX_MEM_memtoreg_2), .ALUResult(MEMALUOut),
    .WrAddr_in(EX_MEM_RegisterRd), .Clk(CLOCK), .RegWrite_2(MEM_WB_RegWrite),
    .MemDataOut(mem_wb_1_memdataout), .MemToReg_2(mem_wb_1_memtoreg_2), .ALUOut(mem_wb_1_aluout),
    .WrAddr_out(MEM_WB_RegisterRd), .Zero(MEM_WB_Zero));
  RAM #(.dataWidth(32), .bus("separate")) ram_1 (
    .addr(bit_extender_4_out), .din(multiplexer_10_out), .data(ram_1_data), .str(EX_MEM_MemWrite),
    .clk(CLOCK), .ld(MemRead));  // open: sel, clr
  Multiplexer #(.width(32), .enable("false")) multiplexer_11 (
    .in0(mem_wb_1_aluout), .in1(mem_wb_1_memdataout), .out(WBWriteData), .sel(mem_wb_1_memtoreg_2));

  // Other names for the same wires on the sheet: EPC[31:0] = EPC_31__0; EX_MEM_Zero = EX_Flush;
  //   ExceptionCause[31:0] = Cause_31__0; ID_EX_Zero = ID_Flush; IF_ID_Zero = IF_Flush; MemWrite = EX_MEM_MemWrite;
  //   RegWr = MEM_WB_RegWrite; WB_MEM_ForwardMem = SWMux; WrAddr[4:0] = MEM_WB_RegisterRd; WrData[31:0] = WBWriteData

  // Notes on the sheet:
  //   contents of rom_1 (hex, n*v repeats v):
  //   20210001 0 0 0 20420001 0 0 0 8000fff 0 0 0 10220019 76*0 10220019 8000fff 53*0 1000ffff
  //   IF/ID
  //   ControlLogic
  //   ID/EX
  //   MEM/WB
  //   Control Signal For StoreWord Mux
endmodule

module _32bit (
  input  Add_Sub_control,
  input  [31:0] in_2,
  input  [31:0] in_3,
  output [31:0] out_4,
  output carry_out
);

  wire adder_1_cout, subtractor_1_bout;
  wire [31:0] adder_1_out, subtractor_1_out;

  Adder #(.width(32)) adder_1 (.a(in_2), .b(in_3), .out(adder_1_out), .cout(adder_1_cout));  // open: cin
  Subtractor #(.width(32)) subtractor_1 (
    .a(in_2), .b(in_3), .out(subtractor_1_out), .bout(subtractor_1_bout));  // open: bin
  Multiplexer #(.width(32), .enable("false")) multiplexer_1 (
    .in0(adder_1_out), .in1(subtractor_1_out), .out(out_4), .sel(Add_Sub_control));
  Multiplexer #(.enable("false")) multiplexer_2 (
    .in0(adder_1_cout), .in1(subtractor_1_bout), .out(carry_out), .sel(Add_Sub_control));
endmodule

module ALU (
  input  [3:0] ALUCtl,
  input  [31:0] A,
  input  [31:0] B,
  input  [4:0] SHamt,
  output [31:0] ALUResult,
  output Zero,
  output Overflow
);

  wire and_2_out, and_3_out, comparator_1_lt, not_1_out, not_2_out, not_4_out, not_5_out, not_6_out,
       or_2_out, or_3_out, xor_1_out;
  wire [31:0] AND_out, bit_extender_1_out, multiplexer_1_out, multiplexer_2_out, multiplexer_4_out,
       n32bit_1_out_4, not_3_out, OR_out, shifter_1_out, shifter_2_out;

  _32bit u_32bit_1 (.Add_Sub_control(ALUCtl[2]), .in_2(A), .in_3(B), .out_4(n32bit_1_out_4));  // open: carry_out
  xor xor_1 (xor_1_out, ALUCtl[2], B[31]);
  not not_1 (not_1_out, A[31]);
  assign OR_out = A | B;  // OR_Gate OR, 32 bits wide
  assign AND_out = A & B;  // AND_Gate AND, 32 bits wide
  Comparator #(.width(32)) comparator_1 (.a(A), .b(B), .lt(comparator_1_lt));  // open: gt, eq
  not not_2 (not_2_out, xor_1_out);
  Shifter #(.width(32)) shifter_1 (.in(B), .\dist (SHamt), .out(shifter_1_out));
  Shifter #(.width(32), .shift("lr")) shifter_2 (.in(B), .\dist (SHamt), .out(shifter_2_out));
  assign not_3_out = ~OR_out;  // NOT_Gate not_3, 32 bits wide
  assign bit_extender_1_out = {{31{1'b0}}, comparator_1_lt};  // Bit_Extender bit_extender_1
  Multiplexer #(.width(32), .enable("false")) multiplexer_1 (
    .in0(AND_out), .in1(OR_out), .out(multiplexer_1_out), .sel(ALUCtl[0]));
  not not_4 (not_4_out, n32bit_1_out_4[31]);
  and and_2 (and_2_out, A[31], not_4_out, xor_1_out);
  and and_3 (and_3_out, not_2_out, n32bit_1_out_4[31], not_1_out);
  Multiplexer #(.width(32), .enable("false")) multiplexer_2 (
    .in0(shifter_1_out), .in1(shifter_2_out), .out(multiplexer_2_out), .sel(ALUCtl[2]));
  Multiplexer #(.select(2), .width(32), .enable("false")) multiplexer_3 (
    .in0(multiplexer_1_out), .in1(multiplexer_4_out), .in2(not_3_out), .in3(multiplexer_2_out),
    .out(ALUResult), .sel({ALUCtl[3], ALUCtl[1]}));
  Multiplexer #(.width(32), .enable("false")) multiplexer_4 (
    .in0(n32bit_1_out_4), .in1(bit_extender_1_out), .out(multiplexer_4_out), .sel(ALUCtl[0]));
  or or_2 (or_2_out, and_2_out, and_3_out);
  not not_5 (not_5_out, ALUCtl[3]);
  not not_6 (not_6_out, ALUCtl[0]);
  and and_4 (Overflow, or_2_out, not_5_out, ALUCtl[1], not_6_out);
  or or_3 (or_3_out, ALUResult[0], ALUResult[1], ALUResult[2], ALUResult[3], ALUResult[4], ALUResult[5], ALUResult[6], ALUResult[7], ALUResult[8], ALUResult[9], ALUResult[10], ALUResult[11], ALUResult[12], ALUResult[13], ALUResult[14], ALUResult[15], ALUResult[16], ALUResult[17], ALUResult[18], ALUResult[19], ALUResult[20], ALUResult[21], ALUResult[22], ALUResult[23], ALUResult[24], ALUResult[25], ALUResult[26], ALUResult[27], ALUResult[28], ALUResult[29], ALUResult[30], ALUResult[31]);
  not not_7 (Zero, or_3_out);

  // Other names for the same wires on the sheet: ALUCtl_1 = ALUCtl[1]; ALUCtl_3 = ALUCtl[3]; ALUCtl_0 = ALUCtl[0];
  //   ALUCtl_2 = ALUCtl[2]
endmodule

module RegisterFile (
  input  clock,
  input  [31:0] WriteData,
  input  [4:0] ReadReg2,
  input  RegWrite,
  input  [4:0] Read_Reg1,
  input  [4:0] WriteReg,
  output [31:0] Read_Data2,
  output [31:0] Read_Data1
);

  wire demultiplexer_1_out0, demultiplexer_1_out1, demultiplexer_1_out2, demultiplexer_1_out3,
       demultiplexer_1_out4, demultiplexer_1_out5, demultiplexer_1_out6, demultiplexer_1_out7,
       demultiplexer_1_out8, demultiplexer_1_out9, demultiplexer_1_out10, demultiplexer_1_out11,
       demultiplexer_1_out12, demultiplexer_1_out13, demultiplexer_1_out14, demultiplexer_1_out15,
       demultiplexer_1_out16, demultiplexer_1_out17, demultiplexer_1_out18, demultiplexer_1_out19,
       demultiplexer_1_out20, demultiplexer_1_out21, demultiplexer_1_out22, demultiplexer_1_out23,
       demultiplexer_1_out24, demultiplexer_1_out25, demultiplexer_1_out26, demultiplexer_1_out27,
       demultiplexer_1_out28, demultiplexer_1_out29, demultiplexer_1_out30, demultiplexer_1_out31;
  wire [31:0] Reg0_2_q, Reg0_3_q, Reg0_4_q, Reg0_5_q, Reg0_6_q, Reg0_7_q, Reg0_8_q, Reg0_9_q, Reg0_10_q,
       Reg0_11_q, Reg0_12_q, Reg0_13_q, Reg0_14_q, Reg0_15_q, Reg0_16_q, Reg0_17_q, Reg0_18_q, Reg0_19_q,
       Reg0_20_q, Reg0_21_q, Reg0_22_q, Reg0_23_q, Reg0_24_q, Reg0_25_q, Reg0_26_q, Reg0_27_q, Reg0_28_q,
       Reg0_29_q, Reg0_30_q, Reg0_31_q, Reg0_32_q, Reg0_q;

  Demultiplexer #(.select(5)) demultiplexer_1 (
    .out0(demultiplexer_1_out0), .out1(demultiplexer_1_out1), .out2(demultiplexer_1_out2),
    .out3(demultiplexer_1_out3), .out4(demultiplexer_1_out4), .out5(demultiplexer_1_out5),
    .out6(demultiplexer_1_out6), .out7(demultiplexer_1_out7), .out8(demultiplexer_1_out8),
    .out9(demultiplexer_1_out9), .out10(demultiplexer_1_out10), .out11(demultiplexer_1_out11),
    .out12(demultiplexer_1_out12), .out13(demultiplexer_1_out13), .out14(demultiplexer_1_out14),
    .out15(demultiplexer_1_out15), .out16(demultiplexer_1_out16), .out17(demultiplexer_1_out17),
    .out18(demultiplexer_1_out18), .out19(demultiplexer_1_out19), .out20(demultiplexer_1_out20),
    .out21(demultiplexer_1_out21), .out22(demultiplexer_1_out22), .out23(demultiplexer_1_out23),
    .out24(demultiplexer_1_out24), .out25(demultiplexer_1_out25), .out26(demultiplexer_1_out26),
    .out27(demultiplexer_1_out27), .out28(demultiplexer_1_out28), .out29(demultiplexer_1_out29),
    .out30(demultiplexer_1_out30), .out31(demultiplexer_1_out31), .in(RegWrite), .sel(WriteReg));  // open: en
  Register #(.width(32)) Reg0 (.D(WriteData), .en(demultiplexer_1_out0), .Q(Reg0_q), .clk(clock));  // open: clr
  Register #(.width(32)) Reg0_2 (.D(WriteData), .en(demultiplexer_1_out4), .Q(Reg0_2_q), .clk(clock));  // open: clr
  Register #(.width(32)) Reg0_3 (.D(WriteData), .en(demultiplexer_1_out8), .Q(Reg0_3_q), .clk(clock));  // open: clr
  Register #(.width(32)) Reg0_4 (.D(WriteData), .en(demultiplexer_1_out12), .Q(Reg0_4_q), .clk(clock));  // open: clr
  Register #(.width(32)) Reg0_5 (.D(WriteData), .en(demultiplexer_1_out16), .Q(Reg0_5_q), .clk(clock));  // open: clr
  Register #(.width(32)) Reg0_6 (.D(WriteData), .en(demultiplexer_1_out20), .Q(Reg0_6_q), .clk(clock));  // open: clr
  Register #(.width(32)) Reg0_7 (.D(WriteData), .en(demultiplexer_1_out24), .Q(Reg0_7_q), .clk(clock));  // open: clr
  Register #(.width(32)) Reg0_8 (.D(WriteData), .en(demultiplexer_1_out28), .Q(Reg0_8_q), .clk(clock));  // open: clr
  Register #(.width(32)) Reg0_9 (.D(WriteData), .en(demultiplexer_1_out1), .Q(Reg0_9_q), .clk(clock));  // open: clr
  Register #(.width(32)) Reg0_10 (.D(WriteData), .en(demultiplexer_1_out5), .Q(Reg0_10_q), .clk(clock));  // open: clr
  Register #(.width(32)) Reg0_11 (.D(WriteData), .en(demultiplexer_1_out9), .Q(Reg0_11_q), .clk(clock));  // open: clr
  Register #(.width(32)) Reg0_12 (.D(WriteData), .en(demultiplexer_1_out13), .Q(Reg0_12_q), .clk(clock));  // open: clr
  Register #(.width(32)) Reg0_13 (.D(WriteData), .en(demultiplexer_1_out17), .Q(Reg0_13_q), .clk(clock));  // open: clr
  Register #(.width(32)) Reg0_14 (.D(WriteData), .en(demultiplexer_1_out21), .Q(Reg0_14_q), .clk(clock));  // open: clr
  Register #(.width(32)) Reg0_15 (.D(WriteData), .en(demultiplexer_1_out25), .Q(Reg0_15_q), .clk(clock));  // open: clr
  Register #(.width(32)) Reg0_16 (.D(WriteData), .en(demultiplexer_1_out29), .Q(Reg0_16_q), .clk(clock));  // open: clr
  Register #(.width(32)) Reg0_17 (.D(WriteData), .en(demultiplexer_1_out2), .Q(Reg0_17_q), .clk(clock));  // open: clr
  Register #(.width(32)) Reg0_18 (.D(WriteData), .en(demultiplexer_1_out6), .Q(Reg0_18_q), .clk(clock));  // open: clr
  Register #(.width(32)) Reg0_19 (.D(WriteData), .en(demultiplexer_1_out10), .Q(Reg0_19_q), .clk(clock));  // open: clr
  Register #(.width(32)) Reg0_20 (.D(WriteData), .en(demultiplexer_1_out14), .Q(Reg0_20_q), .clk(clock));  // open: clr
  Register #(.width(32)) Reg0_21 (.D(WriteData), .en(demultiplexer_1_out18), .Q(Reg0_21_q), .clk(clock));  // open: clr
  Register #(.width(32)) Reg0_22 (.D(WriteData), .en(demultiplexer_1_out22), .Q(Reg0_22_q), .clk(clock));  // open: clr
  Register #(.width(32)) Reg0_23 (.D(WriteData), .en(demultiplexer_1_out26), .Q(Reg0_23_q), .clk(clock), .clr(clock));
  Register #(.width(32)) Reg0_24 (.D(WriteData), .en(demultiplexer_1_out30), .Q(Reg0_24_q), .clk(clock));  // open: clr
  Register #(.width(32)) Reg0_25 (.D(WriteData), .en(demultiplexer_1_out3), .Q(Reg0_25_q), .clk(clock));  // open: clr
  Register #(.width(32)) Reg0_26 (.D(WriteData), .en(demultiplexer_1_out7), .Q(Reg0_26_q), .clk(clock));  // open: clr
  Register #(.width(32)) Reg0_27 (.D(WriteData), .en(demultiplexer_1_out11), .Q(Reg0_27_q), .clk(clock));  // open: clr
  Register #(.width(32)) Reg0_28 (.D(WriteData), .en(demultiplexer_1_out15), .Q(Reg0_28_q), .clk(clock));  // open: clr
  Register #(.width(32)) Reg0_29 (.D(WriteData), .en(demultiplexer_1_out19), .Q(Reg0_29_q), .clk(clock));  // open: clr
  Register #(.width(32)) Reg0_30 (.D(WriteData), .en(demultiplexer_1_out23), .Q(Reg0_30_q), .clk(clock));  // open: clr
  Register #(.width(32)) Reg0_31 (.D(WriteData), .en(demultiplexer_1_out27), .Q(Reg0_31_q), .clk(clock));  // open: clr
  Register #(.width(32)) Reg0_32 (.D(WriteData), .en(demultiplexer_1_out31), .Q(Reg0_32_q), .clk(clock));  // open: clr
  Multiplexer #(.select(5), .width(32)) multiplexer_1 (
    .in0(Reg0_q), .in1(Reg0_9_q), .in2(Reg0_17_q), .in3(Reg0_25_q), .in4(Reg0_2_q), .in5(Reg0_10_q),
    .in6(Reg0_18_q), .in7(Reg0_26_q), .in8(Reg0_3_q), .in9(Reg0_11_q), .in10(Reg0_19_q), .in11(Reg0_27_q),
    .in12(Reg0_4_q), .in13(Reg0_12_q), .in14(Reg0_20_q), .in15(Reg0_28_q), .in16(Reg0_5_q), .in17(Reg0_13_q),
    .in18(Reg0_21_q), .in19(Reg0_29_q), .in20(Reg0_6_q), .in21(Reg0_14_q), .in22(Reg0_22_q),
    .in23(Reg0_30_q), .in24(Reg0_7_q), .in25(Reg0_15_q), .in26(Reg0_23_q), .in27(Reg0_31_q), .in28(Reg0_8_q),
    .in29(Reg0_16_q), .in30(Reg0_24_q), .in31(Reg0_32_q), .out(Read_Data1), .sel(Read_Reg1));  // open: en
  Multiplexer #(.select(5), .width(32)) multiplexer_2 (
    .in0(Reg0_q), .in1(Reg0_9_q), .in2(Reg0_17_q), .in3(Reg0_25_q), .in4(Reg0_2_q), .in5(Reg0_10_q),
    .in6(Reg0_18_q), .in7(Reg0_26_q), .in8(Reg0_3_q), .in9(Reg0_11_q), .in10(Reg0_19_q), .in11(Reg0_27_q),
    .in12(Reg0_4_q), .in13(Reg0_12_q), .in14(Reg0_20_q), .in15(Reg0_28_q), .in16(Reg0_5_q), .in17(Reg0_13_q),
    .in18(Reg0_21_q), .in19(Reg0_29_q), .in20(Reg0_6_q), .in21(Reg0_14_q), .in22(Reg0_22_q),
    .in23(Reg0_30_q), .in24(Reg0_7_q), .in25(Reg0_15_q), .in26(Reg0_23_q), .in27(Reg0_31_q), .in28(Reg0_8_q),
    .in29(Reg0_16_q), .in30(Reg0_24_q), .in31(Reg0_32_q), .out(Read_Data2), .sel(ReadReg2));  // open: en
endmodule

module IF_ID (
  input  [31:0] PC_4_in,
  input  [31:0] in_2,
  input  Clock,
  input  Stall,
  input  Zero,
  output [5:0] Func,
  output [31:0] PC_4_out,
  output [4:0] SHAmt,
  output [15:0] Imm,
  output [4:0] Rd,
  output [4:0] Rt,
  output [5:0] Opcode,
  output [4:0] Rs,
  output [25:0] J_address
);

  wire not_1_out;

  Register #(.width(32)) register_1 (.D(PC_4_in), .Q(PC_4_out), .clk(Clock), .clr(Zero));  // open: en
  not not_1 (not_1_out, Stall);
  Register #(.width(32)) Instruction (
    .D(in_2), .en(not_1_out), .Q({Opcode, J_address[25:16], Imm[15:6], Func}), .clk(Clock), .clr(Zero));

  assign Imm[5:0] = Func;
  assign J_address[15:0] = {Imm[15:6], Func};
  assign Rd = Imm[15:11];
  assign Rs = J_address[25:21];
  assign Rt = J_address[20:16];
  assign SHAmt = Imm[10:6];
endmodule

module Control (
  input  [5:0] FuncBits,
  input  [5:0] Opcode,
  output [3:0] ALUCtl,
  output RegDst,
  output ALUSrc,
  output I_Type,
  output MemRead,
  output MemWrite,
  output RegWrite,
  output MemToReg
);

  wire comparator_1_eq, comparator_2_eq, nand_1_out;
  wire [3:0] ALUCtl_func, ALUCtl_Op;

  FuncBitDecoder funcbitdecoder_1 (
    .Func5(FuncBits[5]), .Func4(FuncBits[4]), .Func3(FuncBits[3]), .Func2(FuncBits[2]), .Func1(FuncBits[1]),
    .Func0(FuncBits[0]), .ALUCtl(ALUCtl_func));
  Comparator #(.width(6)) comparator_1 (.a(Opcode), .b({6{1'b0}}), .eq(comparator_1_eq));  // open: gt, lt
  not not_1 (I_Type, comparator_1_eq);
  Comparator #(.width(6)) comparator_2 (.a({6{1'b0}}), .b(FuncBits), .eq(comparator_2_eq));  // open: gt, lt
  nand nand_1 (nand_1_out, comparator_1_eq, comparator_2_eq);
  InstructionDecoder instructiondecoder_1 (
    .Enable(nand_1_out), .Op5(Opcode[5]), .Op4(Opcode[4]), .Op3(Opcode[3]), .Op2(Opcode[2]), .Op1(Opcode[1]),
    .Op0(Opcode[0]), .RegDst(RegDst), .ALUSrc(ALUSrc), .MemRead(MemRead), .MemWrite(MemWrite),
    .RegWrite(RegWrite), .MemToReg(MemToReg));
  OpCodeDecoder opcodedecoder_1 (.Op5(Opcode[5]), .Op2(Opcode[2]), .Op0(Opcode[0]), .ALUCtl(ALUCtl_Op));
  Multiplexer #(.width(4), .enable("false")) multiplexer_1 (
    .in0(ALUCtl_func), .in1(ALUCtl_Op), .out(ALUCtl), .sel(I_Type));

  // Other names for the same wires on the sheet: Func[5:0] = FuncBits; Op0 = Opcode[0]; Op2 = Opcode[2];
  //   Op5 = Opcode[5]
endmodule

module FuncBitDecoder (
  input  Func5,
  input  Func4,
  input  Func3,
  input  Func2,
  input  Func1,
  input  Func0,
  output [3:0] ALUCtl
);

  wire and_1_out, and_2_out, and_3_out, and_4_out, and_5_out, and_6_out, and_7_out, and_8_out, and_9_out,
       and_10_out, and_11_out, and_12_out, and_13_out, and_14_out, and_15_out, and_16_out, and_17_out,
       and_18_out, and_19_out, not_1_out, not_2_out, not_3_out, not_4_out, not_5_out, not_6_out, not_7_out,
       not_8_out, not_9_out, not_10_out, not_11_out, not_12_out, not_13_out, not_14_out, not_15_out,
       not_16_out, not_17_out, not_18_out, not_19_out, not_20_out, not_21_out, not_22_out, not_23_out,
       not_24_out;

  not not_1 (not_1_out, Func5);
  not not_2 (not_2_out, Func3);
  not not_3 (not_3_out, Func2);
  not not_4 (not_4_out, Func0);
  not not_5 (not_5_out, Func3);
  not not_6 (not_6_out, Func4);
  not not_7 (not_7_out, Func3);
  not not_8 (not_8_out, Func0);
  not not_9 (not_9_out, Func5);
  not not_10 (not_10_out, Func4);
  not not_11 (not_11_out, Func0);
  not not_12 (not_12_out, Func4);
  not not_13 (not_13_out, Func3);
  not not_14 (not_14_out, Func2);
  not not_15 (not_15_out, Func0);
  not not_16 (not_16_out, Func5);
  not not_17 (not_17_out, Func4);
  not not_18 (not_18_out, Func0);
  not not_19 (not_19_out, Func5);
  not not_20 (not_20_out, Func2);
  not not_21 (not_21_out, Func0);
  not not_22 (not_22_out, Func4);
  not not_23 (not_23_out, Func3);
  not not_24 (not_24_out, Func1);
  and and_1 (and_1_out, not_1_out, not_2_out, not_3_out, not_4_out);
  and and_2 (and_2_out, Func5, not_5_out, Func2, Func1, Func0);
  and and_3 (and_3_out, not_6_out, not_7_out, Func1, not_8_out);
  and and_4 (and_4_out, not_9_out, Func2);
  and and_5 (and_5_out, Func2, Func1);
  and and_6 (and_6_out, Func3, Func2);
  and and_7 (and_7_out, Func4, Func2);
  and and_8 (and_8_out, Func5, not_10_out, Func1, not_11_out);
  and and_9 (and_9_out, not_12_out, not_13_out, not_14_out, not_15_out);
  and and_10 (and_10_out, not_16_out, Func2);
  and and_11 (and_11_out, Func3, Func2);
  and and_12 (and_12_out, Func4, Func2);
  and and_13 (and_13_out, Func5, not_17_out, Func1, not_18_out);
  and and_14 (and_14_out, not_19_out, Func1, Func0);
  and and_15 (and_15_out, not_20_out, Func1, Func0);
  and and_16 (and_16_out, Func2, Func1, not_21_out);
  and and_17 (and_17_out, Func3, Func1);
  and and_18 (and_18_out, Func4, Func1);
  and and_19 (and_19_out, Func5, not_22_out, not_23_out, Func2, not_24_out, Func0);
  or or_1 (ALUCtl[3], and_1_out, Func4, and_2_out);
  or or_2 (ALUCtl[2], and_3_out, and_4_out, and_5_out, and_6_out, and_7_out, and_8_out);
  or or_3 (ALUCtl[1], and_9_out, and_10_out, and_11_out, and_12_out, and_13_out);
  or or_4 (ALUCtl[0], and_14_out, and_15_out, and_16_out, and_17_out, and_18_out, and_19_out);
endmodule

module OpCodeDecoder (
  input  Op5,
  input  Op2,
  input  Op0,
  output [3:0] ALUCtl
);

  wire and_1_out, and_2_out, not_1_out, not_2_out, not_3_out, not_4_out;

  not not_1 (not_1_out, Op5);
  not not_2 (not_2_out, Op2);
  not not_3 (not_3_out, Op2);
  not not_4 (not_4_out, Op5);
  and and_1 (and_1_out, not_1_out, not_2_out);
  and and_2 (and_2_out, not_3_out, Op0);
  and and_3 (ALUCtl[0], not_4_out, Op0);
  or or_1 (ALUCtl[1], and_1_out, and_2_out);

  assign ALUCtl[3:2] = 2'b00;
endmodule

module InstructionDecoder (
  input  Enable,
  input  Op5,
  input  Op4,
  input  Op3,
  input  Op2,
  input  Op1,
  input  Op0,
  output RegDst,
  output ALUSrc,
  output MemRead,
  output MemWrite,
  output RegWrite,
  output MemToReg
);

  wire and_1_out, and_2_out, and_3_out, and_4_out, and_5_out, and_6_out, and_7_out, and_8_out, and_9_out,
       and_10_out, and_11_out, and_12_out, not_1_out, not_2_out, not_3_out, not_4_out, not_5_out, not_6_out,
       not_7_out, not_8_out, not_9_out, not_10_out, or_1_out, or_2_out, or_3_out;

  not not_1 (not_1_out, Op3);
  not not_2 (not_2_out, Op1);
  or or_1 (or_1_out, Op0, Op3);
  not not_3 (not_3_out, Op5);
  not not_4 (not_4_out, Op3);
  not not_5 (not_5_out, Op0);
  and and_1 (and_1_out, Op3, Op1);
  not not_6 (not_6_out, Op3);
  not not_7 (not_7_out, Op1);
  not not_8 (not_8_out, Op5);
  not not_9 (not_9_out, Op3);
  not not_10 (not_10_out, Op0);
  and and_2 (and_2_out, not_1_out, not_2_out);
  and and_3 (and_3_out, not_3_out, Op1);
  and and_4 (and_4_out, not_4_out, Op1);
  and and_5 (and_5_out, Op1, not_5_out);
  and and_6 (and_6_out, Op2, Op1);
  and and_7 (and_7_out, Op4, Op1);
  or or_2 (or_2_out, not_6_out, not_7_out);
  and and_8 (and_8_out, not_8_out, Op1);
  and and_9 (and_9_out, not_9_out, Op1);
  and and_10 (and_10_out, Op1, not_10_out);
  and and_11 (and_11_out, Op2, Op1);
  and and_12 (and_12_out, Op4, Op1);
  or or_3 (or_3_out, and_3_out, and_4_out, and_5_out, and_6_out, and_7_out);
  or or_4 (MemToReg, and_8_out, and_9_out, and_10_out, and_11_out, and_12_out);
  and and_13 (RegDst, Enable, and_2_out);
  and and_14 (ALUSrc, Enable, or_1_out);
  and and_15 (MemRead, Enable, or_3_out);
  and and_16 (MemWrite, Enable, and_1_out);
  and and_17 (RegWrite, Enable, or_2_out);
endmodule

module ID_EX (
  input  I_Type,
  input  [3:0] ALUCtl,
  input  [31:0] PC_4_in,
  input  RegDst,
  input  ALUSrc,
  input  [31:0] ReadData1_in,
  input  MemRead,
  input  MemWrite,
  input  [31:0] ReadData2_in,
  input  RegWrite,
  input  MemToReg,
  input  Clk,
  input  [31:0] ExtendedImmediate_in,
  input  Stall,
  input  [4:0] IF_ID_Rt_in,
  input  Zero,
  input  [4:0] IF_ID_Rd_in,
  input  [4:0] SHAmt_in,
  input  [4:0] IF_ID_Rs_in,
  output I_Type_2,
  output [3:0] ALUCtl_2,
  output [31:0] PC_4_out,
  output RegDst_2,
  output ALUSrc_2,
  output [31:0] ReadData1_out,
  output MemRead_2,
  output MemWrite_2,
  output [31:0] ReadData2_out,
  output RegWrite_2,
  output MemToReg_2,
  output [31:0] ExtendedImmediate_out,
  output [4:0] ID_EX_Rt_out,
  output [4:0] ID_EX_Rd_out,
  output [4:0] SHAmt_out,
  output [4:0] ID_EX_Rs_out
);

  wire and_1_out, and_2_out, not_1_out;

  not not_1 (not_1_out, Stall);
  Register #(.width(1)) u_I_Type (.D(I_Type), .Q(I_Type_2), .clk(Clk), .clr(Zero));  // open: en
  Register #(.width(4)) register_1 (.D(ALUCtl), .Q(ALUCtl_2), .clk(Clk), .clr(Zero));  // open: en
  Register #(.width(1)) register_2 (.D(RegDst), .Q(RegDst_2), .clk(Clk), .clr(Zero));  // open: en
  Register #(.width(1)) register_3 (.D(ALUSrc), .Q(ALUSrc_2), .clk(Clk), .clr(Zero));  // open: en
  Register #(.width(1)) register_4 (.D(MemRead), .Q(MemRead_2), .clk(Clk), .clr(Zero));  // open: en
  and and_1 (and_1_out, MemWrite, not_1_out);
  Register #(.width(1)) register_5 (.D(and_1_out), .Q(MemWrite_2), .clk(Clk), .clr(Zero));  // open: en
  and and_2 (and_2_out, RegWrite, not_1_out);
  Register #(.width(1)) register_6 (.D(and_2_out), .Q(RegWrite_2), .clk(Clk), .clr(Zero));  // open: en
  Register #(.width(1)) register_7 (.D(MemToReg), .Q(MemToReg_2), .clk(Clk), .clr(Zero));  // open: en
  Register #(.width(32)) register_8 (.D(PC_4_in), .Q(PC_4_out), .clk(Clk), .clr(Zero));  // open: en
  Register #(.width(32)) register_9 (.D(ReadData1_in), .Q(ReadData1_out), .clk(Clk), .clr(Zero));  // open: en
  Register #(.width(32)) register_10 (.D(ReadData2_in), .Q(ReadData2_out), .clk(Clk), .clr(Zero));  // open: en
  Register #(.width(32)) register_11 (
    .D(ExtendedImmediate_in), .Q(ExtendedImmediate_out), .clk(Clk), .clr(Zero));  // open: en
  Register #(.width(5)) register_12 (.D(IF_ID_Rt_in), .Q(ID_EX_Rt_out), .clk(Clk), .clr(Zero));  // open: en
  Register #(.width(5)) register_13 (.D(IF_ID_Rd_in), .Q(ID_EX_Rd_out), .clk(Clk), .clr(Zero));  // open: en
  Register #(.width(5)) register_14 (.D(SHAmt_in), .Q(SHAmt_out), .clk(Clk), .clr(Zero));  // open: en
  Register #(.width(5)) register_15 (.D(IF_ID_Rs_in), .Q(ID_EX_Rs_out), .clk(Clk), .clr(Zero));  // open: en
endmodule

module EX_MEM (
  input  MemRead,
  input  [31:0] ALUResult,
  input  MemWrite,
  input  RegWrite,
  input  [31:0] RdData2_in,
  input  MemToReg,
  input  [4:0] WrAddr_in,
  input  Clk,
  input  Zero,
  output MemRead_2,
  output [31:0] ALUOut,
  output MemWrite_2,
  output RegWrite_2,
  output [31:0] WrData,
  output MemToReg_2,
  output [4:0] WrAddr_out
);

  Register #(.width(1)) register_1 (.D(MemRead), .Q(MemRead_2), .clk(Clk), .clr(Zero));  // open: en
  Register #(.width(1)) register_2 (.D(MemWrite), .Q(MemWrite_2), .clk(Clk), .clr(Zero));  // open: en
  Register #(.width(1)) register_3 (.D(RegWrite), .Q(RegWrite_2), .clk(Clk), .clr(Zero));  // open: en
  Register #(.width(1)) register_4 (.D(MemToReg), .Q(MemToReg_2), .clk(Clk), .clr(Zero));  // open: en
  Register #(.width(32)) register_5 (.D(ALUResult), .Q(ALUOut), .clk(Clk), .clr(Zero));  // open: en
  Register #(.width(32)) register_6 (.D(RdData2_in), .Q(WrData), .clk(Clk), .clr(Zero));  // open: en
  Register #(.width(5)) WrAddr (.D(WrAddr_in), .Q(WrAddr_out), .clk(Clk), .clr(Zero));  // open: en
endmodule

module MEM_WB (
  input  RegWrite,
  input  [31:0] MemDataIn,
  input  MemToReg,
  input  [31:0] ALUResult,
  input  [4:0] WrAddr_in,
  input  Clk,
  input  Zero,
  output RegWrite_2,
  output [31:0] MemDataOut,
  output MemToReg_2,
  output [31:0] ALUOut,
  output [4:0] WrAddr_out
);

  Register #(.width(1)) register_1 (.D(RegWrite), .Q(RegWrite_2), .clk(Clk), .clr(Zero));  // open: en
  Register #(.width(1)) register_2 (.D(MemToReg), .Q(MemToReg_2), .clk(Clk), .clr(Zero));  // open: en
  Register #(.width(32)) register_3 (.D(MemDataIn), .Q(MemDataOut), .clk(Clk), .clr(Zero));  // open: en
  Register #(.width(32)) register_4 (.D(ALUResult), .Q(ALUOut), .clk(Clk), .clr(Zero));  // open: en
  Register #(.width(5)) register_5 (.D(WrAddr_in), .Q(WrAddr_out), .clk(Clk), .clr(Zero));  // open: en
endmodule

// Forward
module ForwardUnit (
  input  [4:0] ID_EX_RegiterRs,
  input  EX_Mem_MemWrite,
  input  [4:0] ID_EX_RegiterRt,
  input  [4:0] EX_MEM_RegiterRd,
  input  [4:0] MEM_WB_RegiterRd,
  input  EX_MEM_RegWrite,
  input  MEM_WB_RegWrite,
  input  ID_EX_I_Type,
  output [1:0] ForwardA,
  output MEM_WB_ForwardMem,
  output [1:0] ForwardB
);

  wire comparator_5_eq, FWDA_Cond1, FWDA_Cond2, FWDB_Cond1, FWDB_Cond2;

  Comparator #(.width(5)) comparator_1 (.a(ID_EX_RegiterRs), .b(EX_MEM_RegiterRd), .eq(FWDA_Cond1));  // open: gt, lt
  Comparator #(.width(5)) comparator_2 (.a(EX_MEM_RegiterRd), .b(ID_EX_RegiterRt), .eq(FWDB_Cond1));  // open: gt, lt
  Comparator #(.width(5)) comparator_3 (.a(ID_EX_RegiterRs), .b(MEM_WB_RegiterRd), .eq(FWDA_Cond2));  // open: gt, lt
  Comparator #(.width(5)) comparator_4 (.a(ID_EX_RegiterRt), .b(MEM_WB_RegiterRd), .eq(FWDB_Cond2));  // open: gt, lt
  ForwardA forwarda_1 (
    .FWDA_Cond1(FWDA_Cond1), .FWDA_Cond2(FWDA_Cond2), .MEMRegWrite(EX_MEM_RegWrite),
    .WBRegWrite(MEM_WB_RegWrite), .FWDA_1(ForwardA[1]), .FWDA_0(ForwardA[0]));
  Comparator #(.width(5)) comparator_5 (
    .a(EX_MEM_RegiterRd), .b(MEM_WB_RegiterRd), .eq(comparator_5_eq));  // open: gt, lt
  ForwardB forwardb_1 (
    .EXIType(ID_EX_I_Type), .FWDB_Cond1(FWDB_Cond1), .FWDB_Cond2(FWDB_Cond2), .MEMRegWrite(EX_MEM_RegWrite),
    .WBRegWrite(MEM_WB_RegWrite), .FWDB_1(ForwardB[1]), .FWDB_0(ForwardB[0]));
  and and_1 (MEM_WB_ForwardMem, EX_Mem_MemWrite, comparator_5_eq, MEM_WB_RegWrite);

  // Other names for the same wires on the sheet: EX_I_Type = ID_EX_I_Type; MEMRegWrite = EX_MEM_RegWrite;
  //   WBRegWrite = MEM_WB_RegWrite

  // Notes on the sheet:
  //   Previous instruction is either R Type or LW
  //   Only if Sw instruction should use value from WB/WriteData
endmodule

module ForwardA (
  input  FWDA_Cond1,
  input  FWDA_Cond2,
  input  MEMRegWrite,
  input  WBRegWrite,
  output FWDA_1,
  output FWDA_0
);

  and and_1 (FWDA_1, FWDA_Cond1, MEMRegWrite);
  and and_2 (FWDA_0, FWDA_Cond2, WBRegWrite);
endmodule

module ForwardB (
  input  EXIType,
  input  FWDB_Cond1,
  input  FWDB_Cond2,
  input  MEMRegWrite,
  input  WBRegWrite,
  output FWDB_1,
  output FWDB_0
);

  wire and_2_out, and_3_out, not_1_out, not_2_out, not_3_out, not_4_out, not_5_out;

  not not_1 (not_1_out, EXIType);
  not not_2 (not_2_out, EXIType);
  not not_3 (not_3_out, FWDB_Cond1);
  not not_4 (not_4_out, EXIType);
  not not_5 (not_5_out, MEMRegWrite);
  and and_1 (FWDB_1, not_1_out, FWDB_Cond1, MEMRegWrite);
  and and_2 (and_2_out, not_2_out, not_3_out, FWDB_Cond2, WBRegWrite);
  and and_3 (and_3_out, not_4_out, FWDB_Cond2, not_5_out, WBRegWrite);
  or or_1 (FWDB_0, and_2_out, and_3_out);
endmodule

// Stall
module StallCircuit (
  input  IF_ID_MemWrite,
  input  ID_EX_RegWrite,
  input  ID_EX_MemRead,
  input  [4:0] ID_EX_Rt,
  input  [4:0] IF_ID_Rt,
  input  [4:0] IF_ID_Rs,
  input  EX_MEM_MemRead,
  input  Branch,
  input  [4:0] EX_MEM_Rd,
  output Stall
);

  wire and_1_out, and_2_out, and_3_out, comparator_1_eq, comparator_2_eq, comparator_3_eq, comparator_4_eq,
       comparator_5_eq, comparator_6_eq, not_1_out, or_1_out, or_2_out, or_3_out;

  Comparator #(.width(5), .mode("unsigned")) comparator_1 (
    .a(ID_EX_Rt), .b({5{1'b0}}), .eq(comparator_1_eq));  // open: gt, lt
  not not_1 (not_1_out, IF_ID_MemWrite);
  and and_1 (and_1_out, not_1_out, comparator_2_eq);
  Comparator #(.width(5)) comparator_2 (.a(ID_EX_Rt), .b(IF_ID_Rt), .eq(comparator_2_eq));  // open: gt, lt
  Comparator #(.width(5)) comparator_3 (.a(ID_EX_Rt), .b(IF_ID_Rs), .eq(comparator_3_eq));  // open: gt, lt
  Comparator #(.width(5)) comparator_4 (.a(EX_MEM_Rd), .b(IF_ID_Rs), .eq(comparator_4_eq));  // open: gt, lt
  Comparator #(.width(5)) comparator_5 (.a(EX_MEM_Rd), .b(IF_ID_Rt), .eq(comparator_5_eq));  // open: gt, lt
  Comparator #(.width(5), .mode("unsigned")) comparator_6 (
    .a(EX_MEM_Rd), .b({5{1'b0}}), .eq(comparator_6_eq));  // open: gt, lt
  or or_1 (or_1_out, ID_EX_MemRead, Branch);
  or or_2 (or_2_out, and_1_out, comparator_3_eq);
  or or_3 (or_3_out, comparator_4_eq, comparator_5_eq);
  and and_2 (and_2_out, or_1_out, ID_EX_RegWrite, ~comparator_1_eq, or_2_out);  // AND_Gate
  or or_4 (Stall, and_2_out, and_3_out);
  and and_3 (and_3_out, Branch, EX_MEM_MemRead, or_3_out, ~comparator_6_eq);  // AND_Gate

  // Notes on the sheet:
  //   Dont stall if its a sw instruction
endmodule

// ExceptionHandler
module ExceptionHandling (
  input  clk,
  input  Overflow,
  input  [5:0] Instr,
  input  [5:0] Func,
  input  [31:0] PC_4,
  output FLUSH,
  output [31:0] EPC,
  output [31:0] Cause
);

  wire comparator_1_eq, not_1_out, not_2_out, or_1_out, UndefInstr;
  wire [31:0] multiplexer_1_out, undriven;

  UndefinedInstruction undefinedinstruction_1 (
    .o5(Instr[5]), .o4(Instr[4]), .o3(Instr[3]), .o2(Instr[2]), .o1(Instr[1]), .o0(Instr[0]), .f5(Func[5]),
    .f4(Func[4]), .f3(Func[3]), .f2(Func[2]), .f1(Func[1]), .f0(Func[0]), .Undefined(UndefInstr));
  Multiplexer #(.select(2), .width(32), .enable("false")) multiplexer_1 (
    .in0({32{1'b0}}), .in1(32'h1), .in2(32'h2), .in3(undriven), .out(multiplexer_1_out),
    .sel({Overflow, UndefInstr}));
  or or_1 (or_1_out, Overflow, UndefInstr);
  Register #(.width(32)) register_1 (.D(PC_4), .Q(EPC), .clk(FLUSH));  // open: en, clr
  Register #(.width(32)) register_2 (.D(multiplexer_1_out), .Q(Cause), .clk(not_1_out));  // open: en, clr
  not not_1 (not_1_out, clk);
  not not_2 (not_2_out, clk);
  Comparator #(.width(32), .mode("unsigned")) comparator_1 (
    .a(32'h194), .b(PC_4), .eq(comparator_1_eq));  // open: gt, lt
  Register #(.width(1)) register_3 (.D(or_1_out), .Q(FLUSH), .clk(not_2_out), .clr(comparator_1_eq));  // open: en

  // Other names for the same wires on the sheet: Exception = FLUSH

  // Notes on the sheet:
  //   ????
endmodule

module UndefinedInstruction (
  input  o5,
  input  o4,
  input  o3,
  input  o2,
  input  o1,
  input  o0,
  input  f5,
  input  f4,
  input  f3,
  input  f2,
  input  f1,
  input  f0,
  output Undefined
);

  wire and_1_out, and_2_out, and_3_out, and_4_out, and_5_out, and_6_out, and_7_out, and_8_out, and_9_out,
       and_10_out, and_11_out, and_12_out, and_13_out, and_14_out, and_15_out, and_16_out, not_1_out,
       not_2_out, not_3_out, not_4_out, not_5_out, not_6_out, not_7_out, not_8_out, not_9_out, not_10_out,
       not_11_out, not_12_out, not_13_out, not_14_out, not_15_out, not_16_out, not_17_out, not_18_out,
       not_19_out, not_20_out, not_21_out, not_22_out, not_23_out, not_24_out, not_25_out, not_26_out,
       not_27_out, not_28_out, not_29_out, not_30_out, not_31_out, not_32_out, not_33_out, not_34_out,
       not_35_out, not_36_out, not_37_out, not_38_out, not_39_out, not_40_out, not_41_out, not_42_out,
       not_43_out, not_44_out, not_45_out, not_46_out, not_47_out, not_48_out, not_49_out, not_50_out,
       not_51_out, not_52_out, not_53_out, not_54_out, not_55_out, not_56_out, not_57_out, not_58_out,
       not_59_out, not_60_out, not_61_out, not_62_out, not_63_out, not_64_out, not_65_out, or_1_out;

  not not_1 (not_1_out, f4);
  not not_2 (not_2_out, f3);
  not not_3 (not_3_out, f2);
  not not_4 (not_4_out, f1);
  not not_5 (not_5_out, f0);
  not not_6 (not_6_out, f4);
  not not_7 (not_7_out, f3);
  not not_8 (not_8_out, f2);
  not not_9 (not_9_out, f0);
  not not_10 (not_10_out, f4);
  not not_11 (not_11_out, f3);
  not not_12 (not_12_out, f1);
  not not_13 (not_13_out, f0);
  not not_14 (not_14_out, f4);
  not not_15 (not_15_out, f3);
  not not_16 (not_16_out, f1);
  not not_17 (not_17_out, f4);
  not not_18 (not_18_out, f3);
  not not_19 (not_19_out, f4);
  not not_20 (not_20_out, f2);
  not not_21 (not_21_out, f0);
  not not_22 (not_22_out, f5);
  not not_23 (not_23_out, f4);
  not not_24 (not_24_out, f3);
  not not_25 (not_25_out, f2);
  not not_26 (not_26_out, f1);
  not not_27 (not_27_out, f0);
  not not_28 (not_28_out, f5);
  not not_29 (not_29_out, f4);
  not not_30 (not_30_out, f3);
  not not_31 (not_31_out, f2);
  not not_32 (not_32_out, f0);
  and and_1 (and_1_out, f5, not_1_out, not_2_out, not_3_out, not_4_out, not_5_out);
  and and_2 (and_2_out, f5, not_6_out, not_7_out, not_8_out, f1, not_9_out);
  and and_3 (and_3_out, f5, not_10_out, not_11_out, f2, not_12_out, not_13_out);
  and and_4 (and_4_out, f5, not_14_out, not_15_out, f2, not_16_out, f0);
  and and_5 (and_5_out, f5, not_17_out, not_18_out, f2, f1, f0);
  and and_6 (and_6_out, f5, not_19_out, f3, not_20_out, f1, not_21_out);
  and and_7 (and_7_out, not_22_out, not_23_out, not_24_out, not_25_out, not_26_out, not_27_out);
  and and_8 (and_8_out, not_28_out, not_29_out, not_30_out, not_31_out, f1, not_32_out);
  not not_33 (not_33_out, o5);
  not not_34 (not_34_out, o4);
  not not_35 (not_35_out, o3);
  not not_36 (not_36_out, o2);
  not not_37 (not_37_out, o1);
  not not_38 (not_38_out, o0);
  or or_1 (or_1_out, and_1_out, and_2_out, and_3_out, and_4_out, and_5_out, and_6_out, and_7_out, and_8_out);
  not not_39 (not_39_out, o5);
  not not_40 (not_40_out, o4);
  not not_41 (not_41_out, o2);
  not not_42 (not_42_out, o1);
  not not_43 (not_43_out, o0);
  not not_44 (not_44_out, o4);
  not not_45 (not_45_out, o3);
  not not_46 (not_46_out, o2);
  not not_47 (not_47_out, o4);
  not not_48 (not_48_out, o2);
  not not_49 (not_49_out, o5);
  not not_50 (not_50_out, o4);
  not not_51 (not_51_out, o1);
  not not_52 (not_52_out, o0);
  not not_53 (not_53_out, o5);
  not not_54 (not_54_out, o4);
  not not_55 (not_55_out, o1);
  not not_56 (not_56_out, o5);
  not not_57 (not_57_out, o4);
  not not_58 (not_58_out, o3);
  not not_59 (not_59_out, o1);
  not not_60 (not_60_out, o0);
  not not_61 (not_61_out, o5);
  not not_62 (not_62_out, o4);
  not not_63 (not_63_out, o3);
  not not_64 (not_64_out, o2);
  not not_65 (not_65_out, o0);
  and and_9 (and_9_out, not_33_out, not_34_out, not_35_out, not_36_out, not_37_out, not_38_out, or_1_out);
  and and_10 (and_10_out, not_39_out, not_40_out, o3, not_41_out, not_42_out, not_43_out);
  and and_11 (and_11_out, o5, not_44_out, not_45_out, not_46_out, o1, o0);
  and and_12 (and_12_out, o5, not_47_out, o3, not_48_out, o1, o0);
  and and_13 (and_13_out, not_49_out, not_50_out, o3, o2, not_51_out, not_52_out);
  and and_14 (and_14_out, not_53_out, not_54_out, o3, o2, not_55_out, o0);
  and and_15 (and_15_out, not_56_out, not_57_out, not_58_out, o2, not_59_out, not_60_out);
  and and_16 (and_16_out, not_61_out, not_62_out, not_63_out, not_64_out, o1, not_65_out);
  nor nor_1 (Undefined, and_9_out, and_10_out, and_11_out, and_12_out, and_13_out, and_14_out, and_15_out, and_16_out);
endmodule

module Squash (
  input  [31:0] Cause,
  input  Flush,
  input  Jump,
  input  Branch,
  input  Clock,
  input  Stall,
  output IF_ID,
  output ID_EX,
  output EX_MEM,
  output MEM_WB,
  output Exception
);

  wire comparator_1_eq, comparator_2_eq, not_1_out, not_2_out, or_1_out, or_2_out, register_1_q, register_2_q;

  Comparator #(.width(32), .mode("unsigned")) comparator_1 (
    .a(Cause), .b(32'h1), .eq(comparator_1_eq));  // open: gt, lt
  Comparator #(.width(32), .mode("unsigned")) comparator_2 (
    .a(Cause), .b(32'h2), .eq(comparator_2_eq));  // open: gt, lt
  not not_1 (not_1_out, Stall);
  Register #(.width(1)) register_1 (.D(Branch), .en(not_1_out), .Q(register_1_q), .clk(Clock), .clr(register_1_q));
  Register #(.width(1)) register_2 (.D(Jump), .en(not_1_out), .Q(register_2_q), .clk(Clock), .clr(register_2_q));
  or or_1 (or_1_out, comparator_1_eq, register_2_q, register_1_q);
  or or_2 (or_2_out, register_2_q, comparator_2_eq, register_1_q);
  and and_1 (IF_ID, or_1_out, not_2_out);
  and and_2 (ID_EX, or_2_out, not_2_out);
  and and_3 (EX_MEM, 1'b0, not_2_out);
  and and_4 (MEM_WB, 1'b0, not_2_out);
  not not_2 (not_2_out, Stall);

  assign Exception = Flush;
endmodule

module BranchJumpControl (
  input  o5,
  input  o4,
  input  o3,
  input  o2,
  input  o1,
  input  o0,
  output branch,
  output jump
);

  wire not_1_out, not_2_out, not_3_out, not_4_out, not_5_out, not_6_out, not_7_out, not_8_out, not_9_out,
       not_10_out;

  not not_1 (not_1_out, o5);
  not not_2 (not_2_out, o4);
  not not_3 (not_3_out, o3);
  not not_4 (not_4_out, o1);
  not not_5 (not_5_out, o0);
  not not_6 (not_6_out, o5);
  not not_7 (not_7_out, o4);
  not not_8 (not_8_out, o3);
  not not_9 (not_9_out, o2);
  not not_10 (not_10_out, o0);
  and and_1 (branch, not_1_out, not_2_out, not_3_out, o2, not_4_out, not_5_out);
  and and_2 (jump, not_6_out, not_7_out, not_8_out, not_9_out, o1, not_10_out);
endmodule

module Zero (
  input  [31:0] in_1,
  output Zero
);

  wire or_1_out;

  or or_1 (or_1_out, in_1[0], in_1[1], in_1[2], in_1[3], in_1[4], in_1[5], in_1[6], in_1[7], in_1[8], in_1[9], in_1[10], in_1[11], in_1[12], in_1[13], in_1[14], in_1[15], in_1[16], in_1[17], in_1[18], in_1[19], in_1[20], in_1[21], in_1[22], in_1[23], in_1[24], in_1[25], in_1[26], in_1[27], in_1[28], in_1[29], in_1[30], in_1[31]);
  not not_1 (Zero, or_1_out);
endmodule

// BeqForward
module BeqForwardUnit (
  input  MEMRegWrite,
  input  WBRegWrite,
  input  [4:0] IF_ID_Rs,
  input  [4:0] MEM_WB_Rd,
  input  [4:0] EX_MEM_Rd,
  input  [4:0] IF_ID_Rt,
  output [1:0] BeqFWA,
  output [1:0] BeqFWB
);

  wire comparator_1_eq, comparator_2_eq, comparator_3_eq, comparator_4_eq;

  Comparator #(.width(5)) comparator_1 (.a(IF_ID_Rs), .b(MEM_WB_Rd), .eq(comparator_1_eq));  // open: gt, lt
  Comparator #(.width(5)) comparator_2 (.a(IF_ID_Rs), .b(EX_MEM_Rd), .eq(comparator_2_eq));  // open: gt, lt
  Comparator #(.width(5)) comparator_3 (.a(EX_MEM_Rd), .b(IF_ID_Rt), .eq(comparator_3_eq));  // open: gt, lt
  Comparator #(.width(5)) comparator_4 (.a(MEM_WB_Rd), .b(IF_ID_Rt), .eq(comparator_4_eq));  // open: gt, lt
  and and_1 (BeqFWA[0], comparator_1_eq, WBRegWrite);
  and and_2 (BeqFWA[1], WBRegWrite, comparator_2_eq);
  and and_3 (BeqFWB[0], comparator_3_eq, MEMRegWrite);
  and and_4 (BeqFWB[1], MEMRegWrite, comparator_4_eq);

  // Notes on the sheet:
  //   IF/ID.Rs = MEM/WB.Rd
  //   IF/ID.Rs = EX/MEM.Rd
  //   IF/ID.Rt = EX/MEM.Rd
  //   IF/ID.Rt = MEM/WB.Rd
endmodule

module BeqForwardNew (
  input  EX_MEM_ReadMem,
  input  EX_MEM_RegWrite,
  input  [4:0] IF_ID_RegisterRs,
  input  [4:0] EX_MEM_RegisterRd,
  input  [4:0] IF_ID_RegisterRt,
  input  [4:0] MEM_WB_RegisterRd,
  input  MEM_WB_RegWrite,
  output [1:0] ForwardA,
  output [1:0] ForwardB
);

  wire comparator_1_gt, comparator_1_lt, comparator_2_eq, comparator_3_gt, comparator_3_lt, comparator_4_eq,
       comparator_5_gt, comparator_5_lt, comparator_6_eq, comparator_7_gt, comparator_7_lt, comparator_8_eq,
       FA01, FA10, FB01, FB10, or_1_out, or_2_out, or_3_out, or_4_out;

  Comparator #(.width(5), .mode("unsigned")) comparator_1 (
    .a(EX_MEM_RegisterRd), .b({5{1'b0}}), .gt(comparator_1_gt), .lt(comparator_1_lt));  // open: eq
  Comparator #(.width(5), .mode("unsigned")) comparator_2 (
    .a(IF_ID_RegisterRs), .b(EX_MEM_RegisterRd), .eq(comparator_2_eq));  // open: gt, lt
  Comparator #(.width(5), .mode("unsigned")) comparator_3 (
    .a(EX_MEM_RegisterRd), .b({5{1'b0}}), .gt(comparator_3_gt), .lt(comparator_3_lt));  // open: eq
  Comparator #(.width(5), .mode("unsigned")) comparator_4 (
    .a(IF_ID_RegisterRt), .b(EX_MEM_RegisterRd), .eq(comparator_4_eq));  // open: gt, lt
  Comparator #(.width(5), .mode("unsigned")) comparator_5 (
    .a(MEM_WB_RegisterRd), .b({5{1'b0}}), .gt(comparator_5_gt), .lt(comparator_5_lt));  // open: eq
  Comparator #(.width(5), .mode("unsigned")) comparator_6 (
    .a(MEM_WB_RegisterRd), .b(IF_ID_RegisterRs), .eq(comparator_6_eq));  // open: gt, lt
  Comparator #(.width(5), .mode("unsigned")) comparator_7 (
    .a(MEM_WB_RegisterRd), .b({5{1'b0}}), .gt(comparator_7_gt), .lt(comparator_7_lt));  // open: eq
  Comparator #(.width(5), .mode("unsigned")) comparator_8 (
    .a(MEM_WB_RegisterRd), .b(IF_ID_RegisterRt), .eq(comparator_8_eq));  // open: gt, lt
  and and_1 (FA10, EX_MEM_RegWrite, or_1_out, comparator_2_eq);
  or or_1 (or_1_out, comparator_1_gt, comparator_1_lt);
  and and_2 (FB10, EX_MEM_RegWrite, or_2_out, comparator_4_eq);
  or or_2 (or_2_out, comparator_3_gt, comparator_3_lt);
  or or_3 (or_3_out, comparator_5_gt, comparator_5_lt);
  or or_4 (or_4_out, comparator_7_gt, comparator_7_lt);
  and and_3 (FA01, MEM_WB_RegWrite, or_3_out, comparator_6_eq, ~FA10);  // AND_Gate
  and and_4 (FB01, MEM_WB_RegWrite, or_4_out, comparator_8_eq, ~FB10);  // AND_Gate
  Multiplexer #(.select(2), .width(2), .enable("false")) multiplexer_1 (
    .in0(2'b00), .in1(2'b10), .in2(2'b01), .in3(2'b10), .out(ForwardA), .sel({FA01, FA10}));
  Multiplexer #(.select(2), .width(2), .enable("false")) multiplexer_2 (
    .in0(2'b00), .in1(2'b10), .in2(2'b01), .in3(2'b10), .out(ForwardB), .sel({FB01, FB10}));

  // Notes on the sheet:
  //   MEM Hazards
endmodule
